// Logisim project CS1509_U201514305_倪楚锐_CPU_单级中断.circ as structural Verilog: 8 circuits, main circuit cpu
module cpu (
  input  \同步清零信号 ,
  output \与中断屏蔽位与 
);

  wire \_1号中断 , \_1号中断_out , \_1号中断指示 , \_1号中断指示灯 , \_1号中断等待指示 , \_2号中断 , \_2号中断指示 , \_2号中断指示灯 , \_2号中断等待指示 ,
       \_3号中断 , \_3号中断指示 , \_3号中断指示灯 , \_3号中断等待指示 , alu_1_equal, and_1_out, and_2_out, and_3_out, and_4_out,
       and_5_out, and_6_out, CLK, clock_1_out, clock_2_out, control_lbu, d_ff_1_q, d_ff_3_q, ERET, IE, MFC0,
       mfc0_t, nor_1_out, not_1_out, not_2_out, not_3_out, or_1_out, or_2_out, register_3_q, RST, undriven,
       \中断识别_1_中断方波 , \数据选择_we ;
  wire [1:0] control_alu_b, control_dm, undriven_2, \中断识别_1_中断 ;
  wire [2:0] control_rf_din, control_rf_r2, control_rf_w, control_s_ext, \control_条件分支 ;
  wire [3:0] control_alu_op, control_pc, control_rf_r1;
  wire [4:0] rd, \数据选择_rf_r1_out , \数据选择_rf_r2_out , \数据选择_rf_w_out ;
  wire [15:0] \总周期数 , \无条件分支指令数 , \有条件分支成功跳转 , \有条件分支指令数 ;
  wire [31:0] alu_1_result, mips_ram_1_p6, multiplexer_2_out, multiplexer_3_out, PC, PC2, PCnext,
       pull_resistor_1_node, register_1_q, registerfile_1_p7, registerfile_1_p8, SyscallOut, \中断锁存PC , \前PC ,
       \后PC , \数据选择_rf_din_output , \数据选择_s_ext_output ;

  Button \u_总复位  (.out(RST));
  Register #(.width(32)) u_PC (.D(PC2), .en(not_3_out), .Q(PC), .clk(clock_1_out), .clr(RST));
  Clock clock_1 (.out(clock_1_out));
  Button _1 (.out(\_1号中断 ));
  Button _2 (.out(\_2号中断 ));
  Button _3 (.out(\_3号中断 ));
  // Probe on PC
  nor nor_1 (nor_1_out, \_1号中断指示灯 , \_2号中断指示灯 , \_3号中断指示灯 );
  Hex_Digit_Display hex_digit_display_1 (.value(SyscallOut[27:24]));  // open: dp
  Hex_Digit_Display hex_digit_display_2 (.value(SyscallOut[31:28]));  // open: dp
  Hex_Digit_Display hex_digit_display_3 (.value(SyscallOut[23:20]));  // open: dp
  Hex_Digit_Display hex_digit_display_4 (.value(SyscallOut[19:16]));  // open: dp
  LED _1_2 (.in(\_1号中断等待指示 ));
  LED _2_2 (.in(\_2号中断等待指示 ));
  LED _3_2 (.in(\_3号中断等待指示 ));
  Pull_Resistor pull_resistor_1 (.node({pull_resistor_1_node[31:16], rd, pull_resistor_1_node[10:0]}));
  ROM #(.addrWidth(10), .dataWidth(32)) rom_1 (
    .addr(PC[11:2]), .data({pull_resistor_1_node[31:16], rd, pull_resistor_1_node[10:0]}));  // open: sel
  and and_1 (and_1_out, nor_1_out, IE);
  Hex_Digit_Display hex_digit_display_5 (.value(SyscallOut[15:12]));  // open: dp
  Hex_Digit_Display hex_digit_display_6 (.value(SyscallOut[11:8]));  // open: dp
  D_Flip_Flop d_ff_1 (.clk(clock_1_out), .D(rd[0]), .Q(d_ff_1_q), .en(MFC0), .reset(RST));  // open: Qn, preset
  D_Flip_Flop d_ff_2 (.clk(CLK), .D(and_1_out), .reset(undriven));  // open: Q, Qn, preset, en
  Hex_Digit_Display hex_digit_display_7 (.value(SyscallOut[3:0]));  // open: dp
  Hex_Digit_Display hex_digit_display_8 (.value(SyscallOut[7:4]));  // open: dp
  // Probe on \_1号中断 
  control control (
    .op(pull_resistor_1_node[31:26]), .func(pull_resistor_1_node[5:0]), .PC(control_pc), .LBU(control_lbu),
    .RF_R1(control_rf_r1), .RF_R2(control_rf_r2), .RF_W(control_rf_w), .RF_Din(control_rf_din),
    .S_EXT(control_s_ext), .ALU_B(control_alu_b), .DM(control_dm), .ALU_equal(alu_1_equal),
    .BGTZ(alu_1_result[0]), .ALU_OP(control_alu_op), .\条件分支 (\control_条件分支 ),
    .mf(pull_resistor_1_node[25:21]), .MFC0(MFC0), .ERET(ERET));
  selector \u_数据选择  (
    .PC_in(PC), .RF_R1_OUT(\数据选择_rf_r1_out ), .RF_R2_OUT(\数据选择_rf_r2_out ), .DM_OUT(mips_ram_1_p6),
    .RF_W_OUT(\数据选择_rf_w_out ), .ALU(alu_1_result), .RF_Din_OUTPUT(\数据选择_rf_din_output ),
    ._26bitInput({pull_resistor_1_node[25:16], rd, pull_resistor_1_node[10:0]}),
    .S_EXT_OUTPUT(\数据选择_s_ext_output ), .RF_R1(control_rf_r1), .RF_R2(control_rf_r2), .RF_W(control_rf_w),
    .RF_Din(control_rf_din), .S_EXT(control_s_ext), .PC_ctrl(control_pc), .PC_out(PCnext),
    .RF_D1(registerfile_1_p7), .WE(\数据选择_we ), .LBU(control_lbu));
  and and_2 (and_2_out, MFC0, rd[0]);
  Multiplexer #(.select(2), .width(32), .enable("false")) multiplexer_1 (
    .in0(\前PC ), .in1(32'h3370), .in2(32'h3400), .in3(32'h3490), .out(\后PC ), .sel(undriven_2));
  and and_3 (and_3_out, ~rd[0], mfc0_t);  // AND_Gate
  Demultiplexer #(.select(2)) demultiplexer_1 (
    .out1(\_1号中断指示 ), .out2(\_2号中断指示 ), .out3(\_3号中断指示 ), .in(and_3_out), .sel(undriven_2));  // open: out0, en
  Register #(.width(32)) register_1 (.D(PC), .Q(register_1_q), .clk(clock_1_out), .clr(RST));  // open: en
  not not_1 (not_1_out, d_ff_1_q);
  Register #(.width(32)) register_2 (.D(register_1_q), .en(\中断识别_1_中断方波 ), .Q(\中断锁存PC ), .clk(clock_1_out), .clr(RST));
  // Probe on \总周期数 
  // Probe on \无条件分支指令数 
  // Probe on \有条件分支指令数 
  // Probe on \有条件分支成功跳转 
  \中断识别  \u_中断识别_1  (
    .clk(clock_1_out), .IR1(\_1号中断 ), .IR2(\_2号中断 ), .IR3(\_3号中断 ), .\中断等待指示1 (\_1号中断等待指示 ),
    .\中断等待指示2 (\_2号中断等待指示 ), .\中断 (\中断识别_1_中断 ), .\中断等待指示3 (\_3号中断等待指示 ), .IE(and_2_out), .I_end(not_1_out),
    .\中断方波 (\中断识别_1_中断方波 ));
  // RegisterFile registerfile_1: pin names not known; wires that end beside it: \数据选择_rf_din_output , clock_1_out, \数据选择_we , \数据选择_rf_w_out , \数据选择_rf_r1_out , \数据选择_rf_r2_out , registerfile_1_p7, registerfile_1_p8
  // Probe on \中断锁存PC 
  // Probe on nothing
  Clock clock_2 (.out(clock_2_out));
  Button \u__1号中断  (.out(\_1号中断_out ));
  LED \_1号中断等待指示灯  (.in(or_1_out));
  or or_1 (or_1_out, \与中断屏蔽位与 , d_ff_3_q);
  ALU alu_1 (
    .AluOP(control_alu_op), .X(registerfile_1_p7), .Equal(alu_1_equal), .Result(alu_1_result),
    .Y(multiplexer_2_out));  // open: Signed_Overflow, Result_2, UnSigned_Overflow
  Multiplexer #(.select(2), .width(32), .enable("false")) multiplexer_2 (
    .in0({32{1'b0}}), .in1(\数据选择_s_ext_output ), .in2(32'ha), .in3(registerfile_1_p8),
    .out(multiplexer_2_out), .sel(control_alu_b));
  D_Flip_Flop d_ff_3 (.clk(\_1号中断_out ), .D(1'b1), .Q(d_ff_3_q), .reset(\与中断屏蔽位与 ));  // open: Qn, preset, en
  or or_2 (or_2_out, d_ff_3_q, \与中断屏蔽位与 );
  and and_4 (and_4_out, or_2_out, ~\同步清零信号 );  // AND_Gate
  Multiplexer #(.select(2), .width(32), .disabled(0), .enable("false")) multiplexer_3 (
    .in0(PCnext), .in1(32'h3370), .in2(32'h3400), .in3(32'h3490), .out(multiplexer_3_out), .sel(\中断识别_1_中断 ));
  D_Flip_Flop IR1 (.clk(clock_2_out), .D(and_4_out), .Q(\与中断屏蔽位与 ));  // open: Qn, preset, en, reset
  // MIPS_RAM mips_ram_1: pin names not known; wires that end beside it: registerfile_1_p8, control_dm[1], clock_1_out, control_dm[0], RST, mips_ram_1_p6
  Multiplexer #(.width(32), .disabled(0), .enable("false")) multiplexer_4 (
    .in0(multiplexer_3_out), .in1(\中断锁存PC ), .out(PC2), .sel(ERET));
  not not_2 (not_2_out, alu_1_equal);
  Counter #(.width(16), .max('hffff)) counter_1 (
    .load(1'b0), .D({16{1'b0}}), .count(\control_条件分支 [0]), .Q(\无条件分支指令数 ), .clk(clock_1_out), .clr(RST));  // open: carry
  Counter #(.width(16), .max('hffff)) counter_2 (
    .load(1'b0), .D({16{1'b0}}), .count(\control_条件分支 [1]), .Q(\有条件分支指令数 ), .clk(clock_1_out), .clr(RST));  // open: carry
  Counter #(.width(16), .max('hffff)) counter_3 (
    .load(1'b0), .D({16{1'b0}}), .count(\control_条件分支 [2]), .Q(\有条件分支成功跳转 ), .clk(clock_1_out), .clr(RST));  // open: carry
  and and_5 (and_5_out, not_2_out, control_rf_r2[1]);
  and and_6 (and_6_out, alu_1_equal, control_rf_r2[1]);
  Register #(.width(1)) register_3 (.D(and_6_out), .en(not_3_out), .Q(register_3_q), .clk(clock_1_out), .clr(RST));
  Counter #(.width(16), .max('hffff)) counter_4 (
    .load(1'b0), .D({16{1'b0}}), .count(not_3_out), .Q(\总周期数 ), .clk(clock_1_out), .clr(RST));  // open: carry
  Register #(.width(32)) register_4 (
    .D(registerfile_1_p8), .en(and_5_out), .Q(SyscallOut), .clk(clock_1_out), .clr(RST));
  not not_3 (not_3_out, register_3_q);

  // Other names for the same wires on the sheet: rd111 = rd[0]

  // Notes on the sheet:
  //   指令存储器
  //   contents of rom_1 (hex, n*v repeats v):
  //   40020800 20110001 8000c06 20110001 20120002 20130003 8000c0a 20110001 20120002 20130003 8000c0e
  //   20110001 20120002 20130003 8000c12 20110001 20120002 20130003 c000cb9 20100001 20110001 118fc0
  //   112020 20020022 c 118882 12200001 8000c16 112020 20020022 c 20110001 118880 112020 20020022 c
  //   12200001 8000c20 20110001 118fc0 112020 20020022 c 1188c3 112020 20020022 c 118903 112020 20020022 c
  //   118903 112020 20020022 c 118903 112020 20020022 c 118903 112020 20020022 c 118903 112020 20020022 c
  //   118903 112020 20020022 c 118903 112020 20020022 c 20100001 109fc0 139fc3 8021 2012000c 24160003
  //   26100001 3210000f 20080008 20090001 139900 2709825 132020 20020022 c 1094022 1500fff9 22100001
  //   2018000f 2188024 108700 20080008 20090001 139902 2709825 132021 20020022 c 1094022 1500fff9 108702
  //   2c9b022 12c00001 8000c51 4020 1084027 84400 3508ffff 82021 20020022 c 2010ffff 20110000 ae300000
  //   22100001 22310004 ae300000 22100001 22310004 ae300000 22100001 22310004 ae300000 22100001 22310004
  //   ae300000 22100001 22310004 ae300000 22100001 22310004 ae300000 22100001 22310004 ae300000 22100001
  //   22310004 ae300000 22100001 22310004 ae300000 22100001 22310004 ae300000 22100001 22310004 ae300000
  //   22100001 22310004 ae300000 22100001 22310004 ae300000 22100001 22310004 ae300000 22100001 22310004
  //   ae300000 22100001 22310004 22100001 8020 2011003c 8e130000 8e340000 274402a 11000002 ae330000
  //   ae140000 2231fffc 1611fff8 102020 20020022 c 22100004 2011003c 1611fff2 2002000a c 20100000 22100001
  //   102020 20020022 c 22100002 102020 20020022 c 22100003 102020 20020022 c 22100004 102020 20020022 c
  //   22100005 102020 20020022 c 22100006 102020 20020022 c 22100007 102020 20020022 c 22100008 102020
  //   20020022 20020022 c 3e00008 40020000 201d1000 27bdfffc afa40000 27bdfffc afa20000 27bdfffc afb00000
  //   27bdfffc afa80000 27bdfffc afa90000 2020 20020022 c 8020 21080008 20090001 108100 36100001 102021 c
  //   1094022 1500fffa 8fa90000 27bd0004 8fa80000 27bd0004 8fb00000 27bd0004 8fa20000 27bd0004 8fa40000
  //   27bd0004 40020800 42000018 40020000 201d1000 27bdfffc afa40000 27bdfffc afa20000 27bdfffc afb00000
  //   27bdfffc afa80000 27bdfffc afa90000 2020 20020022 c 8020 21080008 20090001 108100 36100002 102021 c
  //   1094022 1500fffa 8fa90000 27bd0004 8fa80000 27bd0004 8fb00000 27bd0004 8fa20000 27bd0004 8fa40000
  //   27bd0004 40020800 42000018 40020000 201d1000 27bdfffc afa40000 27bdfffc afa20000 27bdfffc afb00000
  //   27bdfffc afa80000 27bdfffc afa90000 2020 20020022 c 8020 21080008 20090001 108100 36100003 102021 c
  //   1094022 1500fffa 8fa90000 27bd0004 8fa80000 27bd0004 8fb00000 27bd0004 8fa20000 27bd0004 8fa40000
  //   27bd0004 40020800 42000018
  //   中断信号源及指示电路规范（优先级3>2>1>CPU(0）)
  //   数码管输出
  //   中断信号采样参考电路
  //   Reset 
  //   syscall
endmodule

module control (
  input  ALU_equal,
  input  BGTZ,
  input  [5:0] op,
  input  [5:0] func,
  input  [4:0] mf,
  output [1:0] ALU_B,
  output [3:0] RF_R1,
  output [2:0] RF_R2,
  output [2:0] RF_W,
  output [2:0] RF_Din,
  output [2:0] S_EXT,
  output [1:0] DM,
  output [3:0] PC,
  output LBU,
  output [2:0] \条件分支 ,
  output [3:0] ALU_OP,
  output MFC0,
  output ERET
);

  wire add, addi, addiu, addu, ALU_A_RF_D1, ALU_B_RF_D2, ALU_B_S_EXT, \and , and_3_out, and_4_out, and_5_out,
       and_6_out, and_7_out, and_8_out, andi, beq, bne, comparator_1_eq, comparator_2_eq, comparator_3_eq,
       IM_PC, isR, j, lw, \nor , not_1_out, not_2_out, not_3_out, \or , or_23_out, or_26_out, or_27_out,
       or_28_out, or_29_out, ori, PC_4, PC_offset_PC_4, sll, slt, slti, sltu, sra, srl, sub, \xor , xori;
  wire [5:0] or_1_out;

  assign or_1_out = op | {6{1'b0}};  // OR_Gate or_1, 6 bits wide
  or or_2 (isR, or_1_out[0], or_1_out[1], or_1_out[2], or_1_out[3], or_1_out[4], or_1_out[5]);
  ctrl_r ctr1 (
    .op5(op[5]), .op4(op[4]), .op3(op[3]), .op2(op[2]), .op1(op[1]), .op0(op[0]), .func5(func[5]),
    .func4(func[4]), .func3(func[3]), .func2(func[2]), .func1(func[1]), .func0(func[0]), .add(add),
    .addu(addu), .\and (\and ), .sll(sll), .sra(sra), .sub(sub), .\or (\or ), .\nor (\nor ), .slt(slt),
    .sltu(sltu), .jr(PC[0]));
  ctrl_2 ctr2 (
    .op5(op[5]), .op4(op[4]), .op3(op[3]), .op2(op[2]), .op1(op[1]), .op0(op[0]), .func5(func[5]),
    .func4(func[4]), .func3(func[3]), .func2(func[2]), .func1(func[1]), .func0(func[0]), .srl(srl),
    .addi(addi), .addiu(addiu), .andi(andi), .ori(ori), .lw(lw), .sw(DM[1]), .beq(beq), .bne(bne), .slti(slti));
  ctrl_3 ctr3 (
    .op5(op[5]), .op4(op[4]), .op3(op[3]), .op2(op[2]), .op1(op[1]), .op0(op[0]), .func5(func[5]),
    .func4(func[4]), .func3(func[3]), .func2(func[2]), .func1(func[1]), .func0(func[0]), .j(j),
    .jal(RF_Din[0]), .syscall(RF_R1[1]), .\xor (\xor ), .xori(xori), .lbu(LBU), .bgtz(RF_R1[3]));
  or or_3 (PC_4, add, addu, \and , sra, sub, sll, \or , \nor , slt, sltu, srl, addi, addiu, ori, lw, DM[1], \xor , xori, LBU, slti, andi);
  or or_4 (PC_offset_PC_4, beq, bne, RF_R1[3]);
  or or_5 (PC[1], j, RF_Din[0]);
  or or_6 (RF_R1[2], add, addu, \and , sub, \or , \nor , slt, sltu, addi, addiu, andi, ori, lw, DM[1], beq, bne, slti, \xor , xori, LBU, PC[0]);
  or or_7 (RF_R1[0], sll, sra, srl);
  or or_8 (IM_PC, add, addu, \and , sra, sub, sll, \or , \nor , slt, sltu, srl, addi, addiu, andi, ori, lw, DM[1], beq, bne, slti, j, RF_Din[0], \xor , xori, LBU, RF_R1[3], PC[0]);
  or or_9 (RF_R2[2], add, addu, \and , sub, \or , \nor , slt, sltu, DM[1], beq, bne, \xor );
  Comparator #(.width(6)) comparator_1 (.a(op), .b(6'b010000), .eq(comparator_1_eq));  // open: gt, lt
  Comparator #(.width(5)) comparator_2 (.a(mf), .b({5{1'b0}}), .eq(comparator_2_eq));  // open: gt, lt
  Comparator #(.width(5)) comparator_3 (.a(mf), .b(5'b10000), .eq(comparator_3_eq));  // open: gt, lt
  and and_1 (MFC0, comparator_1_eq, comparator_2_eq);
  and and_2 (ERET, comparator_1_eq, comparator_3_eq);
  or or_10 (S_EXT[0], sll, sra, srl);
  or or_11 (S_EXT[2], j, RF_Din[0]);
  or or_12 (RF_W[2], addi, addiu, andi, ori, lw, slti, xori, LBU);
  or or_13 (RF_W[1], sll, sub, sra, \or , srl, \nor , slt, add, \xor , addu, sltu, \and );
  or or_14 (RF_Din[1], LBU, lw);
  or or_15 (S_EXT[1], lw, addi, DM[1], addiu, slti, andi, xori, ori, LBU);
  or or_16 (RF_Din[2], add, andi, addi, sll, addiu, sra, addu, srl, \and , slt, sub, slti, \or , sltu, ori, \xor , \nor , xori);
  Priority_Encoder #(.select(2)) priority_encoder_1 (
    .in0(1'b1), .in1(ALU_B_S_EXT), .in2(RF_R1[1]), .in3(ALU_B_RF_D2), .out(ALU_B));
  or or_17 (ALU_A_RF_D1, add, andi, addi, sll, addiu, sra, addu, srl, \and , sub, \or , beq, ori, bne, \nor , slt, lw, slti, DM[1], sltu, xori, RF_R1[1], LBU, \xor , RF_R1[3]);
  or or_18 (ALU_B_RF_D2, sub, add, \or , addu, \nor , \and , sltu, beq, \xor , bne, RF_R1[3], slt);
  or or_19 (ALU_B_S_EXT, sll, addi, sra, addiu, srl, andi, ori, slti, lw, xori, DM[1], LBU);
  or or_20 (DM[0], lw, LBU);
  not not_1 (not_1_out, ALU_equal);
  not not_2 (not_2_out, BGTZ);
  not not_3 (not_3_out, ALU_equal);
  and and_3 (and_3_out, beq, not_1_out);
  and and_4 (and_4_out, bne, ALU_equal);
  and and_5 (and_5_out, RF_R1[3], not_2_out);
  and and_6 (and_6_out, beq, ALU_equal);
  and and_7 (and_7_out, bne, not_3_out);
  and and_8 (and_8_out, RF_R1[3], BGTZ);
  or or_21 (PC[3], and_3_out, and_4_out, and_5_out, PC_4);
  or or_22 (PC[2], and_6_out, and_7_out, and_8_out);
  Pull_Resistor pull_resistor_1 (.node(addi));
  Pull_Resistor pull_resistor_2 (.node(add));
  or or_23 (or_23_out, \and , andi);
  or or_24 (\条件分支 [0], j, RF_Din[0], PC[0]);
  or or_25 (\条件分支 [1], beq, bne, RF_R1[3]);
  or or_26 (or_26_out, add, addi, addiu, addu, lw, DM[1], LBU);
  or or_27 (or_27_out, \or , ori);
  or or_28 (or_28_out, \xor , xori);
  or or_29 (or_29_out, RF_R1[3], slt, slti);
  or or_30 (ALU_OP[0], sra, or_26_out, or_23_out, or_28_out, or_29_out);
  or or_31 (ALU_OP[1], srl, sub, or_23_out, \nor , or_29_out);
  or or_32 (ALU_OP[2], or_26_out, sub, or_23_out, sltu);
  or or_33 (ALU_OP[3], or_27_out, or_28_out, \nor , or_29_out, sltu);

  assign RF_R2[1:0] = {RF_R1[1], RF_R1[3]};
  assign RF_W[0] = RF_Din[0];
  assign \条件分支 [2] = PC[2];

  // Other names for the same wires on the sheet: biggerThan0 = BGTZ; DM_read = DM[0]; DM_write = DM[1]; sw = DM[1];
  //   jr = PC[0]; PC_RF_D1 = PC[0]; PC_0XF0000000__addr = PC[1]; pc_PC_4 = PC[3]; Din_PC_4 = RF_Din[0];
  //   jal = RF_Din[0]; W_31 = RF_Din[0]; Din_DM_out = RF_Din[1]; Din_ALU = RF_Din[2]; R1_rt = RF_R1[0];
  //   R1_rs = RF_R1[2]; BGTZ_t = RF_R1[3]; R1_0 = RF_R1[3]; R2_rs = RF_R1[3]; ALU_B_10 = RF_R1[1]; R1_2 = RF_R1[1];
  //   R2_4 = RF_R1[1]; syscall = RF_R1[1]; R2_rt = RF_R2[2]; W_rd = RF_W[1]; W_rt = RF_W[2]; S_EXT_shmat = S_EXT[0];
  //   S_EXT_IMM15 = S_EXT[1]; S_EXT_IMM25 = S_EXT[2]; 无条件分支指令数 = \条件分支 [0]; 有条件分支指令数 = \条件分支 [1]; PC_offset = PC[2];
  //   有条件分支成功跳转 = PC[2]

  // Notes on the sheet:
  //   输入
endmodule

module ctrl_r (
  input  op5,
  input  op4,
  input  op3,
  input  op2,
  input  op1,
  input  op0,
  input  func5,
  input  func4,
  input  func3,
  input  func2,
  input  func1,
  input  func0,
  output add,
  output addu,
  output \and ,
  output sll,
  output sra,
  output sub,
  output \or ,
  output \nor ,
  output slt,
  output sltu,
  output jr
);

  wire not_1_out, not_2_out, not_3_out, not_4_out, not_5_out, not_6_out, not_7_out, not_8_out, not_9_out,
       not_10_out, not_11_out, not_12_out, not_13_out, not_14_out, not_15_out, not_16_out, not_17_out,
       not_18_out, not_19_out, not_20_out, not_21_out, not_22_out, not_23_out, not_24_out, not_25_out,
       not_26_out, not_27_out, not_28_out, not_29_out, not_30_out, not_31_out, not_32_out, not_33_out,
       not_34_out, not_35_out, not_36_out, not_37_out, not_38_out, not_39_out, not_40_out, not_41_out,
       not_42_out, not_43_out, not_44_out, not_45_out, not_46_out, not_47_out, not_48_out, not_49_out,
       not_50_out, not_51_out, not_52_out, not_53_out, not_54_out, not_55_out, not_56_out, not_57_out,
       not_58_out, not_59_out, not_60_out, not_61_out, not_62_out, not_63_out, not_64_out, not_65_out,
       not_66_out, not_67_out, not_68_out, not_69_out, not_70_out, not_71_out, not_72_out, not_73_out,
       not_74_out, not_75_out, not_76_out, not_77_out, not_78_out, not_79_out, not_80_out, not_81_out,
       not_82_out, not_83_out, not_84_out, not_85_out, not_86_out, not_87_out, not_88_out, not_89_out,
       not_90_out, not_91_out, not_92_out, not_93_out, not_94_out, not_95_out, not_96_out, not_97_out,
       not_98_out, not_99_out, not_100_out, not_101_out, not_102_out, not_103_out, not_104_out, not_105_out,
       not_106_out, not_107_out, not_108_out;

  not not_1 (not_1_out, op5);
  not not_2 (not_2_out, op4);
  not not_3 (not_3_out, op3);
  not not_4 (not_4_out, op2);
  not not_5 (not_5_out, op1);
  not not_6 (not_6_out, op0);
  not not_7 (not_7_out, func4);
  not not_8 (not_8_out, func3);
  not not_9 (not_9_out, func2);
  not not_10 (not_10_out, func1);
  not not_11 (not_11_out, func0);
  not not_12 (not_12_out, op5);
  not not_13 (not_13_out, op4);
  not not_14 (not_14_out, op3);
  not not_15 (not_15_out, op2);
  not not_16 (not_16_out, op1);
  not not_17 (not_17_out, op0);
  not not_18 (not_18_out, func4);
  not not_19 (not_19_out, func3);
  not not_20 (not_20_out, func2);
  not not_21 (not_21_out, func1);
  not not_22 (not_22_out, op5);
  not not_23 (not_23_out, op4);
  not not_24 (not_24_out, op3);
  not not_25 (not_25_out, op2);
  not not_26 (not_26_out, op1);
  not not_27 (not_27_out, op0);
  not not_28 (not_28_out, func4);
  not not_29 (not_29_out, func3);
  not not_30 (not_30_out, func1);
  not not_31 (not_31_out, func0);
  not not_32 (not_32_out, op5);
  not not_33 (not_33_out, op4);
  not not_34 (not_34_out, op3);
  not not_35 (not_35_out, op2);
  not not_36 (not_36_out, op1);
  not not_37 (not_37_out, op0);
  not not_38 (not_38_out, func5);
  not not_39 (not_39_out, func4);
  not not_40 (not_40_out, func3);
  not not_41 (not_41_out, func2);
  not not_42 (not_42_out, func1);
  not not_43 (not_43_out, func0);
  not not_44 (not_44_out, op5);
  not not_45 (not_45_out, op4);
  not not_46 (not_46_out, op3);
  not not_47 (not_47_out, op2);
  not not_48 (not_48_out, op1);
  not not_49 (not_49_out, op0);
  not not_50 (not_50_out, func5);
  not not_51 (not_51_out, func4);
  not not_52 (not_52_out, func3);
  not not_53 (not_53_out, func2);
  not not_54 (not_54_out, op5);
  not not_55 (not_55_out, op4);
  not not_56 (not_56_out, op3);
  not not_57 (not_57_out, op2);
  not not_58 (not_58_out, op1);
  not not_59 (not_59_out, op0);
  not not_60 (not_60_out, func4);
  not not_61 (not_61_out, func3);
  not not_62 (not_62_out, func2);
  not not_63 (not_63_out, func0);
  not not_64 (not_64_out, op5);
  not not_65 (not_65_out, op4);
  not not_66 (not_66_out, op3);
  not not_67 (not_67_out, op2);
  not not_68 (not_68_out, op1);
  not not_69 (not_69_out, op0);
  not not_70 (not_70_out, func4);
  not not_71 (not_71_out, func3);
  not not_72 (not_72_out, func1);
  not not_73 (not_73_out, op5);
  not not_74 (not_74_out, op4);
  not not_75 (not_75_out, op3);
  not not_76 (not_76_out, op2);
  not not_77 (not_77_out, op1);
  not not_78 (not_78_out, op0);
  not not_79 (not_79_out, func4);
  not not_80 (not_80_out, func3);
  not not_81 (not_81_out, op5);
  not not_82 (not_82_out, op4);
  not not_83 (not_83_out, op3);
  not not_84 (not_84_out, op2);
  not not_85 (not_85_out, op1);
  not not_86 (not_86_out, op0);
  not not_87 (not_87_out, func4);
  not not_88 (not_88_out, func2);
  not not_89 (not_89_out, func0);
  not not_90 (not_90_out, op5);
  not not_91 (not_91_out, op4);
  not not_92 (not_92_out, op3);
  not not_93 (not_93_out, op2);
  not not_94 (not_94_out, op1);
  not not_95 (not_95_out, op0);
  not not_96 (not_96_out, func4);
  not not_97 (not_97_out, func2);
  not not_98 (not_98_out, op5);
  not not_99 (not_99_out, op4);
  not not_100 (not_100_out, op3);
  not not_101 (not_101_out, op2);
  not not_102 (not_102_out, op1);
  not not_103 (not_103_out, op0);
  not not_104 (not_104_out, func5);
  not not_105 (not_105_out, func4);
  not not_106 (not_106_out, func2);
  not not_107 (not_107_out, func1);
  not not_108 (not_108_out, func0);
  and and_1 (add, not_1_out, not_2_out, not_3_out, not_4_out, not_5_out, not_6_out, func5, not_7_out, not_8_out, not_9_out, not_10_out, not_11_out);
  and and_2 (addu, not_12_out, not_13_out, not_14_out, not_15_out, not_16_out, not_17_out, func5, not_18_out, not_19_out, not_20_out, not_21_out, func0);
  and and_3 (\and , not_22_out, not_23_out, not_24_out, not_25_out, not_26_out, not_27_out, func5, not_28_out, not_29_out, func2, not_30_out, not_31_out);
  and and_4 (sll, not_32_out, not_33_out, not_34_out, not_35_out, not_36_out, not_37_out, not_38_out, not_39_out, not_40_out, not_41_out, not_42_out, not_43_out);
  and and_5 (sra, not_44_out, not_45_out, not_46_out, not_47_out, not_48_out, not_49_out, not_50_out, not_51_out, not_52_out, not_53_out, func1, func0);
  and and_6 (sub, not_54_out, not_55_out, not_56_out, not_57_out, not_58_out, not_59_out, func5, not_60_out, not_61_out, not_62_out, func1, not_63_out);
  and and_7 (\or , not_64_out, not_65_out, not_66_out, not_67_out, not_68_out, not_69_out, func5, not_70_out, not_71_out, func2, not_72_out, func0);
  and and_8 (\nor , not_73_out, not_74_out, not_75_out, not_76_out, not_77_out, not_78_out, func5, not_79_out, not_80_out, func2, func1, func0);
  and and_9 (slt, not_81_out, not_82_out, not_83_out, not_84_out, not_85_out, not_86_out, func5, not_87_out, func3, not_88_out, func1, not_89_out);
  and and_10 (sltu, not_90_out, not_91_out, not_92_out, not_93_out, not_94_out, not_95_out, func5, not_96_out, func3, not_97_out, func1, func0);
  and and_11 (jr, not_98_out, not_99_out, not_100_out, not_101_out, not_102_out, not_103_out, not_104_out, not_105_out, func3, not_106_out, not_107_out, not_108_out);
endmodule

module ctrl_2 (
  input  op5,
  input  op4,
  input  op3,
  input  op2,
  input  op1,
  input  op0,
  input  func5,
  input  func4,
  input  func3,
  input  func2,
  input  func1,
  input  func0,
  output srl,
  output addi,
  output addiu,
  output andi,
  output ori,
  output lw,
  output sw,
  output beq,
  output bne,
  output slti
);

  wire not_1_out, not_2_out, not_3_out, not_4_out, not_5_out, not_6_out, not_7_out, not_8_out, not_9_out,
       not_10_out, not_11_out, not_12_out, not_13_out, not_14_out, not_15_out, not_16_out, not_17_out,
       not_18_out, not_19_out, not_20_out, not_21_out, not_22_out, not_23_out, not_24_out, not_25_out,
       not_26_out, not_27_out, not_28_out, not_29_out, not_30_out, not_31_out, not_32_out, not_33_out,
       not_34_out, not_35_out, not_36_out, not_37_out, not_38_out, not_39_out, not_40_out, not_41_out,
       not_42_out, not_43_out, not_44_out, not_45_out;

  not not_1 (not_1_out, op5);
  not not_2 (not_2_out, op4);
  not not_3 (not_3_out, op3);
  not not_4 (not_4_out, op2);
  not not_5 (not_5_out, op1);
  not not_6 (not_6_out, op0);
  not not_7 (not_7_out, func5);
  not not_8 (not_8_out, func4);
  not not_9 (not_9_out, func3);
  not not_10 (not_10_out, func2);
  not not_11 (not_11_out, func0);
  not not_12 (not_12_out, op5);
  not not_13 (not_13_out, op4);
  not not_14 (not_14_out, op2);
  not not_15 (not_15_out, op1);
  not not_16 (not_16_out, op0);
  not not_17 (not_17_out, op5);
  not not_18 (not_18_out, op4);
  not not_19 (not_19_out, op2);
  not not_20 (not_20_out, op1);
  not not_21 (not_21_out, op5);
  not not_22 (not_22_out, op4);
  not not_23 (not_23_out, op1);
  not not_24 (not_24_out, op0);
  not not_25 (not_25_out, op5);
  not not_26 (not_26_out, op4);
  not not_27 (not_27_out, op1);
  not not_28 (not_28_out, op4);
  not not_29 (not_29_out, op3);
  not not_30 (not_30_out, op2);
  not not_31 (not_31_out, op4);
  not not_32 (not_32_out, op2);
  not not_33 (not_33_out, op5);
  not not_34 (not_34_out, op4);
  not not_35 (not_35_out, op3);
  not not_36 (not_36_out, op1);
  not not_37 (not_37_out, op0);
  not not_38 (not_38_out, op5);
  not not_39 (not_39_out, op4);
  not not_40 (not_40_out, op3);
  not not_41 (not_41_out, op1);
  not not_42 (not_42_out, op5);
  not not_43 (not_43_out, op4);
  not not_44 (not_44_out, op2);
  not not_45 (not_45_out, op0);
  and and_1 (srl, not_1_out, not_2_out, not_3_out, not_4_out, not_5_out, not_6_out, not_7_out, not_8_out, not_9_out, not_10_out, func1, not_11_out);
  and and_2 (addi, not_12_out, not_13_out, op3, not_14_out, not_15_out, not_16_out);
  and and_3 (addiu, not_17_out, not_18_out, op3, not_19_out, not_20_out, op0);
  and and_4 (andi, not_21_out, not_22_out, op3, op2, not_23_out, not_24_out);
  and and_5 (ori, not_25_out, not_26_out, op3, op2, not_27_out, op0);
  and and_6 (lw, op5, not_28_out, not_29_out, not_30_out, op1, op0);
  and and_7 (sw, op5, not_31_out, op3, not_32_out, op1, op0);
  and and_8 (beq, not_33_out, not_34_out, not_35_out, op2, not_36_out, not_37_out);
  and and_9 (bne, not_38_out, not_39_out, not_40_out, op2, not_41_out, op0);
  and and_10 (slti, not_42_out, not_43_out, op3, not_44_out, op1, not_45_out);
endmodule

module ctrl_3 (
  input  op5,
  input  op4,
  input  op3,
  input  op2,
  input  op1,
  input  op0,
  input  func5,
  input  func4,
  input  func3,
  input  func2,
  input  func1,
  input  func0,
  output j,
  output jal,
  output syscall,
  output \xor ,
  output xori,
  output lbu,
  output bgtz
);

  wire not_1_out, not_2_out, not_3_out, not_4_out, not_5_out, not_6_out, not_7_out, not_8_out, not_9_out,
       not_10_out, not_11_out, not_12_out, not_13_out, not_14_out, not_15_out, not_16_out, not_17_out,
       not_18_out, not_19_out, not_20_out, not_21_out, not_22_out, not_23_out, not_24_out, not_25_out,
       not_26_out, not_27_out, not_28_out, not_29_out, not_30_out, not_31_out, not_32_out, not_33_out,
       not_34_out, not_35_out, not_36_out, not_37_out, not_38_out;

  not not_1 (not_1_out, op5);
  not not_2 (not_2_out, op4);
  not not_3 (not_3_out, op3);
  not not_4 (not_4_out, op2);
  not not_5 (not_5_out, op0);
  not not_6 (not_6_out, op5);
  not not_7 (not_7_out, op4);
  not not_8 (not_8_out, op3);
  not not_9 (not_9_out, op2);
  not not_10 (not_10_out, op5);
  not not_11 (not_11_out, op4);
  not not_12 (not_12_out, op3);
  not not_13 (not_13_out, op2);
  not not_14 (not_14_out, op1);
  not not_15 (not_15_out, op0);
  not not_16 (not_16_out, func5);
  not not_17 (not_17_out, func4);
  not not_18 (not_18_out, func1);
  not not_19 (not_19_out, func0);
  not not_20 (not_20_out, op5);
  not not_21 (not_21_out, op4);
  not not_22 (not_22_out, op3);
  not not_23 (not_23_out, op2);
  not not_24 (not_24_out, op1);
  not not_25 (not_25_out, op0);
  not not_26 (not_26_out, func4);
  not not_27 (not_27_out, func3);
  not not_28 (not_28_out, func0);
  not not_29 (not_29_out, op5);
  not not_30 (not_30_out, op4);
  not not_31 (not_31_out, op0);
  not not_32 (not_32_out, op4);
  not not_33 (not_33_out, op3);
  not not_34 (not_34_out, op1);
  not not_35 (not_35_out, op0);
  not not_36 (not_36_out, op5);
  not not_37 (not_37_out, op4);
  not not_38 (not_38_out, op3);
  and and_1 (j, not_1_out, not_2_out, not_3_out, not_4_out, op1, not_5_out);
  and and_2 (jal, not_6_out, not_7_out, not_8_out, not_9_out, op1, op0);
  and and_3 (syscall, not_10_out, not_11_out, not_12_out, not_13_out, not_14_out, not_15_out, not_16_out, not_17_out, func3, func2, not_18_out, not_19_out);
  and and_4 (\xor , not_20_out, not_21_out, not_22_out, not_23_out, not_24_out, not_25_out, func5, not_26_out, not_27_out, func2, func1, not_28_out);
  and and_5 (xori, not_29_out, not_30_out, op3, op2, op1, not_31_out);
  and and_6 (lbu, op5, not_32_out, not_33_out, op2, not_34_out, not_35_out);
  and and_7 (bgtz, not_36_out, not_37_out, not_38_out, op2, op1, op0);
endmodule

module selector (
  input  [3:0] PC_ctrl,
  input  [2:0] RF_W,
  input  [2:0] RF_Din,
  input  [3:0] RF_R1,
  input  [2:0] RF_R2,
  input  [2:0] S_EXT,
  input  LBU,
  input  [31:0] DM_OUT,
  input  [31:0] ALU,
  input  [31:0] PC_in,
  input  [25:0] _26bitInput,
  input  [31:0] RF_D1,
  output [4:0] RF_W_OUT,
  output [4:0] RF_R1_OUT,
  output [31:0] PC_out,
  output WE,
  output [31:0] RF_Din_OUTPUT,
  output [31:0] S_EXT_OUTPUT,
  output [4:0] RF_R2_OUT
);

  wire adder_2_cout, adder_3_cout;
  wire [1:0] priority_encoder_1_out, priority_encoder_2_out, priority_encoder_3_out, priority_encoder_4_out,
       priority_encoder_5_out, priority_encoder_6_out;
  wire [31:0] _26to32extend, adder_1_out, adder_2_out, adder_3_out, bit_extender_1_out, bit_extender_2_out,
       bit_extender_3_out;

  Priority_Encoder #(.select(2)) priority_encoder_1 (
    .in0(1'b1), .in1(RF_R2[2]), .in2(RF_R2[1]), .in3(RF_R2[0]), .out(priority_encoder_1_out));  // open: gs, en_out, en_in
  Priority_Encoder #(.select(2), .disabled(0)) priority_encoder_2 (
    .in0(1'b1), .in1(RF_W[0]), .in2(RF_W[1]), .in3(RF_W[2]), .out(priority_encoder_2_out));  // open: gs, en_out, en_in
  Adder #(.width(32)) adder_1 (.a(32'h4), .b(PC_in), .out(adder_1_out));  // open: cin, cout
  Priority_Encoder #(.select(2), .disabled(0)) priority_encoder_3 (
    .in0(RF_R1[3]), .in1(RF_R1[0]), .in2(RF_R1[1]), .in3(RF_R1[2]), .out(priority_encoder_3_out));  // open: gs, en_out, en_in
  Multiplexer #(.select(2), .width(5), .disabled(0), .enable("false")) multiplexer_1 (
    .in0({5{1'b0}}), .in1(_26bitInput[20:16]), .in2(5'b00010), .in3(_26bitInput[25:21]), .out(RF_R1_OUT),
    .sel(priority_encoder_3_out));
  Multiplexer #(.select(2), .width(5), .enable("false")) multiplexer_2 (
    .in0({5{1'b0}}), .in1(_26bitInput[20:16]), .in2(5'b00100), .in3(_26bitInput[25:21]), .out(RF_R2_OUT),
    .sel(priority_encoder_1_out));
  Multiplexer #(.select(2), .width(5), .disabled(0), .enable("false")) multiplexer_3 (
    .in0({5{1'b0}}), .in1({5{1'b1}}), .in2(_26bitInput[15:11]), .in3(_26bitInput[20:16]), .out(RF_W_OUT),
    .sel(priority_encoder_2_out));
  Priority_Encoder #(.select(2)) priority_encoder_4 (
    .in0(RF_Din[2]), .in1(RF_Din[1]), .in2(RF_Din[0]), .in3(LBU), .out(priority_encoder_4_out));  // open: gs, en_out, en_in
  Multiplexer #(.select(2), .width(32), .disabled(0), .enable("false")) multiplexer_4 (
    .in0(ALU), .in1(DM_OUT), .in2(adder_1_out), .in3({{24{1'b0}}, DM_OUT[7:0]}), .out(RF_Din_OUTPUT),
    .sel(priority_encoder_4_out));
  Pull_Resistor pull_resistor_1 (.node(priority_encoder_3_out));
  or or_1 (WE, RF_W[2], RF_W[1], RF_W[0]);
  assign bit_extender_1_out = {{27{1'b0}}, _26bitInput[10:6]};  // Bit_Extender bit_extender_1
  assign bit_extender_2_out = {{16{_26bitInput[15]}}, _26bitInput[15:0]};  // Bit_Extender bit_extender_2
  assign bit_extender_3_out = {{14{_26bitInput[15]}}, {_26bitInput[15:0], 2'b00}};  // Bit_Extender bit_extender_3
  Adder #(.width(32)) adder_2 (.a(PC_in), .b(32'h4), .out(adder_2_out), .cout(adder_2_cout));  // open: cin
  Priority_Encoder #(.select(2), .disabled(0)) priority_encoder_5 (
    .in0(1'b1), .in1(S_EXT[0]), .in2(S_EXT[1]), .in3(S_EXT[2]), .out(priority_encoder_5_out));  // open: gs, en_out, en_in
  Multiplexer #(.select(2), .width(32), .disabled(0), .enable("false")) multiplexer_5 (
    .in0({32{1'b0}}), .in1(bit_extender_1_out), .in2(bit_extender_2_out), .in3(_26to32extend),
    .out(S_EXT_OUTPUT), .sel(priority_encoder_5_out));
  assign _26to32extend = {{4{_26bitInput[25]}}, {_26bitInput, 2'b00}};  // Bit_Extender bit_extender_4
  Priority_Encoder #(.select(2)) priority_encoder_6 (
    .in0(PC_ctrl[3]), .in1(PC_ctrl[2]), .in2(PC_ctrl[1]), .in3(PC_ctrl[0]), .out(priority_encoder_6_out));  // open: gs, en_out, en_in
  Adder #(.width(32)) adder_3 (
    .a(adder_2_out), .b(bit_extender_3_out), .out(adder_3_out), .cout(adder_3_cout));  // open: cin
  Multiplexer #(.select(2), .width(32), .disabled(0), .enable("false")) multiplexer_6 (
    .in0(adder_2_out), .in1(adder_3_out), .in2({PC_in[31:28], _26bitInput, 2'b00}), .in3(RF_D1),
    .out(PC_out), .sel(priority_encoder_6_out));
  Pull_Resistor pull_resistor_2 (.node(priority_encoder_6_out));
  // also tied to GND on the sheet: {adder_2_cout, adder_3_cout}

  // Other names for the same wires on the sheet: _16Immediate[15:0] = _26bitInput[15:0];
  //   _26Immediate[25:0] = _26bitInput; _28Immediate[27:2] = _26bitInput; func[5:0] = _26bitInput[5:0];
  //   instructionInput[25:0] = _26bitInput; shmat[4:0] = _26bitInput[10:6]; RD[4:0] = _26bitInput[15:11];
  //   RT[4:0] = _26bitInput[20:16]; RS[4:0] = _26bitInput[25:21]; PC[31:0] = PC_in; PC_RF_D1 = PC_ctrl[0];
  //   PC_0XF0000000__addr = PC_ctrl[1]; PC_offset = PC_ctrl[2]; pc_PC_4 = PC_ctrl[3]; Din_PC_4 = RF_Din[0];
  //   Din_DM_out = RF_Din[1]; Din_ALU = RF_Din[2]; R1_rt = RF_R1[0]; R1_2 = RF_R1[1]; R1_rs = RF_R1[2];
  //   R1_0 = RF_R1[3]; R2_rs = RF_R2[0]; R2_4 = RF_R2[1]; R2_rt = RF_R2[2]; W_31 = RF_W[0]; W_rd = RF_W[1];
  //   W_rt = RF_W[2]; S_EXT_shmat = S_EXT[0]; S_EXT_IMM15 = S_EXT[1]; S_EXT_IMM25 = S_EXT[2]
endmodule

module \中断识别  (
  input  clk,
  input  IR1,
  input  IR2,
  input  IR3,
  input  IE,
  input  I_end,
  output \中断等待指示1 ,
  output \中断等待指示2 ,
  output [1:0] \中断 ,
  output \中断等待指示3 ,
  output \中断方波 
);

  wire and_1_out, and_2_out, and_3_out, \中断产生_1_与中断屏蔽位与 , \中断产生_2_与中断屏蔽位与 , \中断产生_3_与中断屏蔽位与 ;

  \中断产生  \u_中断产生_1  (.clk(clk), .\中断 (IR1), .\同步清零信号 (IE), .\中断等待指示 (\中断等待指示1 ), .\与中断屏蔽位与 (\中断产生_1_与中断屏蔽位与 ));
  \中断产生  \u_中断产生_2  (.clk(clk), .\中断 (IR2), .\同步清零信号 (IE), .\中断等待指示 (\中断等待指示2 ), .\与中断屏蔽位与 (\中断产生_2_与中断屏蔽位与 ));
  \中断产生  \u_中断产生_3  (.clk(clk), .\中断 (IR3), .\同步清零信号 (IE), .\中断等待指示 (\中断等待指示3 ), .\与中断屏蔽位与 (\中断产生_3_与中断屏蔽位与 ));
  and and_1 (and_1_out, \中断产生_1_与中断屏蔽位与 , ~I_end);  // AND_Gate
  and and_2 (and_2_out, \中断产生_2_与中断屏蔽位与 , ~I_end);  // AND_Gate
  and and_3 (and_3_out, \中断产生_3_与中断屏蔽位与 , ~I_end);  // AND_Gate
  Priority_Encoder #(.select(2), .disabled(0)) priority_encoder_1 (
    .in0(1'b0), .in1(and_1_out), .in2(and_2_out), .in3(and_3_out), .out(\中断 ), .gs(\中断方波 ), .en_in(1'b1));  // open: en_out
  Pull_Resistor pull_resistor_1 (.node(\中断 ));
endmodule

module \中断产生  (
  input  clk,
  input  \中断 ,
  input  \同步清零信号 ,
  output \与中断屏蔽位与 ,
  output \中断等待指示 
);

  wire and_1_out, d_ff_1_q, or_2_out;

  D_Flip_Flop d_ff_1 (.clk(\中断 ), .D(1'b1), .Q(d_ff_1_q), .reset(\与中断屏蔽位与 ));  // open: Qn, preset, en
  or or_1 (\中断等待指示 , \与中断屏蔽位与 , d_ff_1_q);
  or or_2 (or_2_out, d_ff_1_q, \与中断屏蔽位与 );
  and and_1 (and_1_out, or_2_out, ~\同步清零信号 );  // AND_Gate
  D_Flip_Flop IR1 (.clk(clk), .D(and_1_out), .Q(\与中断屏蔽位与 ));  // open: Qn, preset, en, reset

  // Notes on the sheet:
  //   中断信号采样参考电路
  //   Reset 
endmodule
