// Logisim project CS1509_U201514305_倪楚锐_redirect.circ as structural Verilog: 16 circuits, main circuit cpu
module cpu (
);

  wire alu_1_equal, and_1_out, and_3_out, and_4_out, bubble, clock_1_out, conflict_dectect_1_a_w1,
       conflict_dectect_1_a_w2, conflict_dectect_1_b_w1, conflict_dectect_1_b_w2,
       conflict_dectect_1_conflict, control_lbu, control_loaduse, EX_MEM_end_out, EX_MEM_lbu_out,
       ID_EX_lbu_out, JMP, loadUse1, loadUse2, MEM_WB_syscall_out, not_1_out, not_2_out, not_3_out,
       not_4_out, or_1_out, or_2_out, register_2_q, RST, wb_1_we, WE, we_rw_1_we;
  wire [1:0] control_alu_b, control_dm, control_pc_01, control_src_op, \control_条件分支 , EX_MEM_dm_out,
       EX_MEM_srcop_out, ID_EX_alub_out, ID_EX_dm_out, ID_EX_srcop_out;
  wire [2:0] control_rf_din, control_rf_r2, control_rf_w, control_s_ext, EX_MEM_rfdin_out, EX_MEM_rfw_out,
       ID_EX_r2_2, ID_EX_rfdin_out, ID_EX_rfw_out, \条件分支 ;
  wire [3:0] control_alu_op, control_branch, control_rf_r1, ID_EX_branch_out, ID_EX_op_2, PC_CTRL;
  wire [4:0] AAA, BBB, EX_MEM_ra_out, EX_MEM_rb_out, ID_EX_ra_out, ID_EX_rb_out, rw, wb_1_rf_w_out,
       we_rw_1_rf_w_out;
  wire [15:0] \loadUse数 , \总周期数 , \无条件分支指令数 , \有条件分支成功跳转 , \有条件分支指令数 ;
  wire [25:0] _26b, EX_MEM_instr26_out;
  wire [31:0] A, alu_1_result, B, EX_MEM_bin_out, EX_MEM_pc_out, EX_MEM_result_out, ID_EX_b_in_2,
       ID_EX_ext_2, ID_EX_pc_out, IF_ID_out, IF_ID_pc_out, IF_ID_pcp4_out, mips_ram_1_p9, multiplexer_1_out,
       npc_1_pc_4, npc_1_pc_out, oldPC_4, PC_q, registerfile_1_p7, registerfile_1_p8, RF_D1, rom_1_data,
       SyscallOut, wb_1_rf_din_output, writeBack, \数据选择_s_ext_output ;

  Button \u_总复位  (.out(RST));
  LED led_1 (.in(not_1_out));
  not not_1 (not_1_out, not_4_out);
  npc npc_1 (
    .PC_ctrl(PC_CTRL), .PC_in(PC_q), .PC_out(npc_1_pc_out), ._26bitInput(_26b), .JMP(JMP), .oldPC_4(oldPC_4),
    .PC_4(npc_1_pc_4), .RF_D1(RF_D1));
  Clock clock_1 (.out(clock_1_out));
  not not_2 (not_2_out, bubble);
  Hex_Digit_Display hex_digit_display_1 (.value(SyscallOut[31:28]));  // open: dp
  Hex_Digit_Display hex_digit_display_2 (.value(SyscallOut[27:24]));  // open: dp
  and and_1 (and_1_out, not_2_out, not_4_out);
  Hex_Digit_Display hex_digit_display_3 (.value(SyscallOut[23:20]));  // open: dp
  Hex_Digit_Display hex_digit_display_4 (.value(SyscallOut[19:16]));  // open: dp
  // Probe on PC_q
  Register #(.width(32)) PC (.D(npc_1_pc_out), .en(and_1_out), .Q(PC_q), .clk(clock_1_out), .clr(RST));
  Hex_Digit_Display hex_digit_display_5 (.value(SyscallOut[15:12]));  // open: dp
  Hex_Digit_Display hex_digit_display_6 (.value(SyscallOut[11:8]));  // open: dp
  Hex_Digit_Display hex_digit_display_7 (.value(SyscallOut[3:0]));  // open: dp
  Hex_Digit_Display hex_digit_display_8 (.value(SyscallOut[7:4]));  // open: dp
  // Probe on rom_1_data
  // Probe on IF_ID_out
  ROM #(.addrWidth(10), .dataWidth(32)) rom_1 (.addr(PC_q[11:2]), .data(rom_1_data));  // open: sel
  \if  IF_ID (
    .rst(RST), .clk(clock_1_out), .in(rom_1_data), .out(IF_ID_out), .en(and_1_out), .PC_in(PC_q),
    .PC_out(IF_ID_pc_out), .clear(JMP), .PCp4_in(npc_1_pc_4), .PCp4_out(IF_ID_pcp4_out));
  Counter #(.width(16), .max('hffff)) counter_1 (
    .load(1'b0), .D({16{1'b0}}), .count(bubble), .Q(\loadUse数 ), .clk(clock_1_out), .clr(RST));  // open: carry
  // Probe on BBB
  // Probe on AAA
  Pull_Resistor pull_resistor_1 (.node(IF_ID_out));
  // Probe on \总周期数 
  // Probe on \无条件分支指令数 
  // Probe on \有条件分支指令数 
  // Probe on \有条件分支成功跳转 
  control control (
    .op(IF_ID_out[31:26]), .func(IF_ID_out[5:0]), .PC_01(control_pc_01), .LBU(control_lbu),
    .RF_R1(control_rf_r1), .RF_R2(control_rf_r2), .RF_W(control_rf_w), .RF_Din(control_rf_din),
    .S_EXT(control_s_ext), .ALU_B(control_alu_b), .DM(control_dm), .ALU_OP(control_alu_op),
    .src_op(control_src_op), .\条件分支 (\control_条件分支 ), .branch(control_branch), .loadUse(control_loaduse));
  selector \u_数据选择  (
    .RF_R1_OUT(AAA), .RF_R2_OUT(BBB), ._26bitInput(IF_ID_out[25:0]), .S_EXT_OUTPUT(\数据选择_s_ext_output ),
    .RF_R1(control_rf_r1), .RF_R2(control_rf_r2), .S_EXT(control_s_ext));
  conflict_dectect conflict_dectect_1 (
    .RA(AAA), .RB(BBB), .srcOP(control_src_op), .WE1(we_rw_1_we), .rw1(we_rw_1_rf_w_out), .WE2(wb_1_we),
    .rw2(wb_1_rf_w_out), .conflict(conflict_dectect_1_conflict), .B_W1(conflict_dectect_1_b_w1),
    .B_W2(conflict_dectect_1_b_w2), .A_W1(conflict_dectect_1_a_w1), .A_W2(conflict_dectect_1_a_w2));
  // Probe on \loadUse数 
  redirect redirect (
    .B_W1(conflict_dectect_1_b_w1), .B_W2(conflict_dectect_1_b_w2), .A_W1(conflict_dectect_1_a_w1),
    .A_W2(conflict_dectect_1_a_w2), .A(registerfile_1_p7), .B(registerfile_1_p8), .wb2(wb_1_rf_din_output),
    .wb1(alu_1_result), .redir_Aout(A), .redir_Bout(B));
  // RegisterFile registerfile_1: pin names not known; wires that end beside it: writeBack, clock_1_out, WE, rw, AAA, BBB, registerfile_1_p7, registerfile_1_p8, RST, clock_1_out
  or or_1 (or_1_out, loadUse2, loadUse1);
  id ID_EX (
    .rst(RST), .clk(clock_1_out), .dm(control_dm), .ALUB(control_alu_b), .A_in(A), .ext(\数据选择_s_ext_output ),
    .B_in(B), .OP(control_alu_op), .R2(control_rf_r2), .dm_out(ID_EX_dm_out), .ALUB_out(ID_EX_alub_out),
    .A_out(RF_D1), .ext_2(ID_EX_ext_2), .B_in_2(ID_EX_b_in_2), .OP_2(ID_EX_op_2), .R2_2(ID_EX_r2_2),
    .en(not_4_out), .PC_out(ID_EX_pc_out), .PC_in(IF_ID_pc_out), .rfdin_out(ID_EX_rfdin_out),
    .rf_in(control_rf_din), .lbu_in(control_lbu), .lbu_out(ID_EX_lbu_out), .rfw_in(control_rf_w),
    .rfw_out(ID_EX_rfw_out), .instr26_in(IF_ID_out[25:0]), .instr26_out(_26b), .RA(AAA), .RB(BBB),
    .srcOP(control_src_op), .RA_out(ID_EX_ra_out), .RB_out(ID_EX_rb_out), .srcOP_out(ID_EX_srcop_out),
    .clear(or_2_out), .PCctrl_in(control_pc_01), .PCctrl_out(PC_CTRL[1:0]), .temp_in(\control_条件分支 ),
    .temp_out(\条件分支 [1:0]), .PCp4_in(IF_ID_pcp4_out), .PCp4_out(oldPC_4), .branch(control_branch),
    .branch_out(ID_EX_branch_out), .loadUse_in(control_loaduse), .loadUser_out(loadUse1));
  and and_2 (bubble, conflict_dectect_1_conflict, or_1_out);
  PCctrl pcctrl_1 (
    .branch(ID_EX_branch_out), .\条件分支 (\条件分支 [2]), .ALU_equal(alu_1_equal), .BGTZ(alu_1_result[0]),
    .PC_23(PC_CTRL[3:2]));
  Multiplexer #(.select(2), .width(32), .enable("false")) multiplexer_1 (
    .in0({32{1'b0}}), .in1(ID_EX_ext_2), .in2(32'ha), .in3(ID_EX_b_in_2), .out(multiplexer_1_out),
    .sel(ID_EX_alub_out));
  or or_2 (or_2_out, bubble, JMP);
  ALU alu_1 (
    .AluOP(ID_EX_op_2), .X(RF_D1), .Equal(alu_1_equal), .Result(alu_1_result), .Y(multiplexer_1_out));  // open: Signed_Overflow, Result_2, UnSigned_Overflow
  not not_3 (not_3_out, alu_1_equal);
  and and_3 (and_3_out, not_3_out, ID_EX_r2_2[1]);
  and and_4 (and_4_out, alu_1_equal, ID_EX_r2_2[1]);
  Counter #(.width(16), .max('hffff)) counter_2 (
    .load(1'b0), .D({16{1'b0}}), .count(not_4_out), .Q(\总周期数 ), .clk(clock_1_out), .clr(RST));  // open: carry
  Register #(.width(32)) register_1 (.D(ID_EX_b_in_2), .en(and_3_out), .Q(SyscallOut), .clk(clock_1_out), .clr(RST));
  Register #(.width(1)) register_2 (.D(and_4_out), .en(not_4_out), .Q(register_2_q), .clk(clock_1_out), .clr(RST));
  WE_RW we_rw_1 (.WE(we_rw_1_we), .RF_W_OUT(we_rw_1_rf_w_out), ._26bitInput(_26b), .RF_W(ID_EX_rfw_out));
  ex EX_MEM (
    .dm_out(EX_MEM_dm_out), .result_out(EX_MEM_result_out), .end_out(EX_MEM_end_out),
    .Bin_out(EX_MEM_bin_out), .dm(ID_EX_dm_out), .result(alu_1_result), .\end (register_2_q),
    .Bin(ID_EX_b_in_2), .rst(RST), .clk(clock_1_out), .en(not_4_out), .PC_out(EX_MEM_pc_out),
    .PC_in(ID_EX_pc_out), .rf_in(ID_EX_rfdin_out), .rfdin_out(EX_MEM_rfdin_out), .lbu_in(ID_EX_lbu_out),
    .lbu_out(EX_MEM_lbu_out), .rfw_in(ID_EX_rfw_out), .rfw_out(EX_MEM_rfw_out), .instr26_in(_26b),
    .instr26_out(EX_MEM_instr26_out), .RA(ID_EX_ra_out), .RB(ID_EX_rb_out), .srcOP(ID_EX_srcop_out),
    .RA_out(EX_MEM_ra_out), .RB_out(EX_MEM_rb_out), .srcOP_out(EX_MEM_srcop_out), .loadUse_in(loadUse1),
    .loadUser_out(loadUse2));
  // MIPS_RAM mips_ram_1: pin names not known; wires that end beside it: EX_MEM_ra_out, EX_MEM_rb_out, EX_MEM_srcop_out, EX_MEM_bin_out, EX_MEM_dm_out[1], clock_1_out, EX_MEM_dm_out[0], RST, mips_ram_1_p9
  // Probe on mips_ram_1_p9
  wb wb_1 (
    .PC_in(EX_MEM_pc_out), .RF_Din_OUTPUT(wb_1_rf_din_output), .DM_OUT(mips_ram_1_p9),
    .ALU(EX_MEM_result_out), .RF_Din(EX_MEM_rfdin_out), .LBU(EX_MEM_lbu_out), .RF_W_OUT(wb_1_rf_w_out),
    .WE(wb_1_we), .RF_W(EX_MEM_rfw_out), ._26bitInput(EX_MEM_instr26_out));
  mem MEM_WB (
    .rst(RST), .clk(clock_1_out), .syscall(EX_MEM_end_out), .syscall_out(MEM_WB_syscall_out), .en(not_4_out),
    .WE_out(WE), .writeBack_out_2(writeBack), .rw_out(rw), .WE(wb_1_we), .writeBack_out(wb_1_rf_din_output),
    .rw(wb_1_rf_w_out));
  not not_4 (not_4_out, MEM_WB_syscall_out);
  Counter #(.width(16), .max('hffff)) counter_3 (
    .load(1'b0), .D({16{1'b0}}), .count(\条件分支 [0]), .Q(\无条件分支指令数 ), .clk(clock_1_out), .clr(RST));  // open: carry
  Counter #(.width(16), .max('hffff)) counter_4 (
    .load(1'b0), .D({16{1'b0}}), .count(\条件分支 [1]), .Q(\有条件分支指令数 ), .clk(clock_1_out), .clr(RST));  // open: carry
  Counter #(.width(16), .max('hffff)) counter_5 (
    .load(1'b0), .D({16{1'b0}}), .count(\条件分支 [2]), .Q(\有条件分支成功跳转 ), .clk(clock_1_out), .clr(RST));  // open: carry

  // Notes on the sheet:
  //   数码管输出应该用寄存器锁存，否则显示数据只能一闪而过
  //   取指令
  //   可以通过项目增加Logisim库的方式将前几次实验完成的电路作为子电路引入到本电路中使用
  //   指令存储器
  //   数码管输出
  //   contents of rom_1 (hex, n*v repeats v):
  //   20110001 8000c05 20110001 20120002 20130003 8000c09 20110001 20120002 20130003 8000c0d 20110001
  //   20120002 20130003 8000c11 20110001 20120002 20130003 c000cb8 20100001 20110001 118fc0 112020
  //   20020022 c 118882 12200001 8000c15 112020 20020022 c 20110001 118880 112020 20020022 c 12200001
  //   8000c1f 20110001 118fc0 112020 20020022 c 1188c3 112020 20020022 c 118903 112020 20020022 c 118903
  //   112020 20020022 c 118903 112020 20020022 c 118903 112020 20020022 c 118903 112020 20020022 c 118903
  //   112020 20020022 c 118903 112020 20020022 c 20100001 109fc0 139fc3 8021 2012000c 24160003 26100001
  //   3210000f 20080008 20090001 139900 2709825 132020 20020022 c 1094022 1500fff9 22100001 2018000f
  //   2188024 108700 20080008 20090001 139902 2709825 132021 20020022 c 1094022 1500fff9 108702 2c9b022
  //   12c00001 8000c50 4020 1084027 84400 3508ffff 82021 20020022 c 2010ffff 20110000 ae300000 22100001
  //   22310004 ae300000 22100001 22310004 ae300000 22100001 22310004 ae300000 22100001 22310004 ae300000
  //   22100001 22310004 ae300000 22100001 22310004 ae300000 22100001 22310004 ae300000 22100001 22310004
  //   ae300000 22100001 22310004 ae300000 22100001 22310004 ae300000 22100001 22310004 ae300000 22100001
  //   22310004 ae300000 22100001 22310004 ae300000 22100001 22310004 ae300000 22100001 22310004 ae300000
  //   22100001 22310004 22100001 8020 2011003c 8e130000 8e340000 274402a 11000002 ae330000 ae140000
  //   2231fffc 1611fff8 102020 20020022 c 22100004 2011003c 1611fff2 2002000a c 20100000 22100001 102020
  //   20020022 c 22100002 102020 20020022 c 22100003 102020 20020022 c 22100004 102020 20020022 c 22100005
  //   102020 20020022 c 22100006 102020 20020022 c 22100007 102020 20020022 c 22100008 102020 20020022
  //   20020022 c 3e00008
  //   总复位信号应将除ROM以外所有存储组件全部清零
  //   译码
  //   执行
  //   syscall
  //   访存
  //   写回
endmodule

module control (
  input  [5:0] op,
  input  [5:0] func,
  output [1:0] ALU_B,
  output [3:0] RF_R1,
  output [2:0] RF_R2,
  output [2:0] RF_W,
  output [2:0] RF_Din,
  output [2:0] S_EXT,
  output [1:0] DM,
  output [1:0] PC_01,
  output LBU,
  output [1:0] \条件分支 ,
  output [3:0] ALU_OP,
  output loadUse,
  output [3:0] branch,
  output [1:0] src_op
);

  wire add, addi, addiu, addu, ALU_A_RF_D1, ALU_B_RF_D2, ALU_B_S_EXT, \and , andi, IM_PC, isR, j, lw, \nor ,
       \or , or_25_out, or_26_out, or_27_out, or_28_out, or_29_out, ori, PC_offset_PC_4, sll, slt, slti,
       sltu, sra, srl, sub, \xor , xori;
  wire [5:0] or_1_out;

  assign or_1_out = op | {6{1'b0}};  // OR_Gate or_1, 6 bits wide
  or or_2 (isR, or_1_out[0], or_1_out[1], or_1_out[2], or_1_out[3], or_1_out[4], or_1_out[5]);
  ctrl_r ctr1 (
    .op5(op[5]), .op4(op[4]), .op3(op[3]), .op2(op[2]), .op1(op[1]), .op0(op[0]), .func5(func[5]),
    .func4(func[4]), .func3(func[3]), .func2(func[2]), .func1(func[1]), .func0(func[0]), .add(add),
    .addu(addu), .\and (\and ), .sll(sll), .sra(sra), .sub(sub), .\or (\or ), .\nor (\nor ), .slt(slt),
    .sltu(sltu), .jr(PC_01[0]));
  ctrl_2 ctr2 (
    .op5(op[5]), .op4(op[4]), .op3(op[3]), .op2(op[2]), .op1(op[1]), .op0(op[0]), .func5(func[5]),
    .func4(func[4]), .func3(func[3]), .func2(func[2]), .func1(func[1]), .func0(func[0]), .srl(srl),
    .addi(addi), .addiu(addiu), .andi(andi), .ori(ori), .lw(lw), .sw(DM[1]), .beq(branch[0]),
    .bne(branch[1]), .slti(slti));
  ctrl_3 ctr3 (
    .op5(op[5]), .op4(op[4]), .op3(op[3]), .op2(op[2]), .op1(op[1]), .op0(op[0]), .func5(func[5]),
    .func4(func[4]), .func3(func[3]), .func2(func[2]), .func1(func[1]), .func0(func[0]), .j(j),
    .jal(RF_Din[0]), .syscall(RF_R1[1]), .\xor (\xor ), .xori(xori), .lbu(LBU), .bgtz(branch[2]));
  or or_3 (branch[3], add, addu, \and , sra, sub, sll, \or , \nor , slt, sltu, srl, addi, addiu, ori, lw, DM[1], \xor , xori, LBU, slti, andi);
  or or_4 (PC_offset_PC_4, branch[0], branch[1], branch[2]);
  or or_5 (PC_01[1], j, RF_Din[0]);
  or or_6 (RF_R1[2], add, addu, \and , sub, \or , \nor , slt, sltu, addi, addiu, andi, ori, lw, DM[1], branch[0], branch[1], slti, \xor , xori, LBU, PC_01[0]);
  or or_7 (RF_R1[0], sll, sra, srl);
  or or_8 (IM_PC, add, addu, \and , sra, sub, sll, \or , \nor , slt, sltu, srl, addi, addiu, andi, ori, lw, DM[1], branch[0], branch[1], slti, j, RF_Din[0], \xor , xori, LBU, branch[2], PC_01[0]);
  or or_9 (RF_R2[2], add, addu, \and , sub, \or , \nor , slt, sltu, DM[1], branch[0], branch[1], \xor );
  or or_10 (S_EXT[0], sll, sra, srl);
  or or_11 (S_EXT[2], j, RF_Din[0]);
  or or_12 (RF_W[2], addi, addiu, andi, ori, lw, slti, xori, LBU);
  or or_13 (RF_W[1], sll, sub, sra, \or , srl, \nor , slt, add, \xor , addu, sltu, \and );
  or or_14 (RF_Din[1], LBU, lw);
  or or_15 (S_EXT[1], lw, addi, DM[1], addiu, slti, andi, xori, ori, LBU);
  or or_16 (RF_Din[2], add, andi, addi, sll, addiu, sra, addu, srl, \and , slt, sub, slti, \or , sltu, ori, \xor , \nor , xori);
  Priority_Encoder #(.select(2)) priority_encoder_1 (
    .in0(1'b1), .in1(ALU_B_S_EXT), .in2(RF_R1[1]), .in3(ALU_B_RF_D2), .out(ALU_B));
  or or_17 (ALU_A_RF_D1, add, andi, addi, sll, addiu, sra, addu, srl, \and , sub, \or , branch[0], ori, branch[1], \nor , slt, lw, slti, DM[1], sltu, xori, RF_R1[1], LBU, \xor , branch[2]);
  or or_18 (ALU_B_RF_D2, sub, add, \or , addu, \nor , \and , sltu, branch[0], \xor , branch[1], branch[2], slt);
  or or_19 (ALU_B_S_EXT, sll, addi, sra, addiu, srl, andi, ori, slti, lw, xori, DM[1], LBU);
  or or_20 (DM[0], lw, LBU);
  or or_21 (src_op[0], sll, add, sra, addi, srl, addiu, sub, addu, \or , \and , ori, andi, \nor , lw, PC_01[0], DM[1], RF_R1[1], branch[0], \xor , branch[1], xori, slt, LBU, slti, branch[2], sltu);
  or or_22 (src_op[1], add, \or , addu, \nor , \and , DM[1], sub, sltu, branch[0], RF_R1[1], branch[1], \xor , slt, branch[2]);
  or or_23 (\条件分支 [0], j, RF_Din[0], PC_01[0]);
  or or_24 (\条件分支 [1], branch[0], branch[1], branch[2]);
  or or_25 (or_25_out, \and , andi);
  or or_26 (or_26_out, add, addi, addiu, addu, lw, DM[1], LBU);
  or or_27 (or_27_out, \or , ori);
  or or_28 (or_28_out, \xor , xori);
  or or_29 (or_29_out, branch[2], slt, slti);
  or or_30 (loadUse, lw, LBU);
  or or_31 (ALU_OP[0], sra, or_26_out, or_25_out, or_28_out, or_29_out);
  or or_32 (ALU_OP[1], srl, sub, or_25_out, \nor , or_29_out);
  or or_33 (ALU_OP[2], or_26_out, sub, or_25_out, sltu);
  or or_34 (ALU_OP[3], or_27_out, or_28_out, \nor , or_29_out, sltu);

  assign RF_R1[3] = branch[2];
  assign RF_R2[1:0] = {RF_R1[1], branch[2]};
  assign RF_W[0] = RF_Din[0];

  // Other names for the same wires on the sheet: beq = branch[0]; bne = branch[1]; BGTZ = branch[2]; R1_0 = branch[2];
  //   R2_rs = branch[2]; PC_4 = branch[3]; DM_read = DM[0]; DM_write = DM[1]; sw = DM[1]; jr = PC_01[0];
  //   PC_RF_D1 = PC_01[0]; PC_0XF0000000__addr = PC_01[1]; Din_PC_4 = RF_Din[0]; jal = RF_Din[0]; W_31 = RF_Din[0];
  //   Din_DM_out = RF_Din[1]; Din_ALU = RF_Din[2]; R1_rt = RF_R1[0]; R1_rs = RF_R1[2]; ALU_B_10 = RF_R1[1];
  //   R1_2 = RF_R1[1]; R2_4 = RF_R1[1]; syscall = RF_R1[1]; R2_rt = RF_R2[2]; W_rd = RF_W[1]; W_rt = RF_W[2];
  //   S_EXT_shmat = S_EXT[0]; S_EXT_IMM15 = S_EXT[1]; S_EXT_IMM25 = S_EXT[2]; src1 = src_op[0]; src2 = src_op[1];
  //   无条件分支指令数 = \条件分支 [0]; 有条件分支指令数 = \条件分支 [1]

  // Notes on the sheet:
  //   输入
endmodule

module ctrl_r (
  input  op5,
  input  op4,
  input  op3,
  input  op2,
  input  op1,
  input  op0,
  input  func5,
  input  func4,
  input  func3,
  input  func2,
  input  func1,
  input  func0,
  output add,
  output addu,
  output \and ,
  output sll,
  output sra,
  output sub,
  output \or ,
  output \nor ,
  output slt,
  output sltu,
  output jr
);

  wire not_1_out, not_2_out, not_3_out, not_4_out, not_5_out, not_6_out, not_7_out, not_8_out, not_9_out,
       not_10_out, not_11_out, not_12_out, not_13_out, not_14_out, not_15_out, not_16_out, not_17_out,
       not_18_out, not_19_out, not_20_out, not_21_out, not_22_out, not_23_out, not_24_out, not_25_out,
       not_26_out, not_27_out, not_28_out, not_29_out, not_30_out, not_31_out, not_32_out, not_33_out,
       not_34_out, not_35_out, not_36_out, not_37_out, not_38_out, not_39_out, not_40_out, not_41_out,
       not_42_out, not_43_out, not_44_out, not_45_out, not_46_out, not_47_out, not_48_out, not_49_out,
       not_50_out, not_51_out, not_52_out, not_53_out, not_54_out, not_55_out, not_56_out, not_57_out,
       not_58_out, not_59_out, not_60_out, not_61_out, not_62_out, not_63_out, not_64_out, not_65_out,
       not_66_out, not_67_out, not_68_out, not_69_out, not_70_out, not_71_out, not_72_out, not_73_out,
       not_74_out, not_75_out, not_76_out, not_77_out, not_78_out, not_79_out, not_80_out, not_81_out,
       not_82_out, not_83_out, not_84_out, not_85_out, not_86_out, not_87_out, not_88_out, not_89_out,
       not_90_out, not_91_out, not_92_out, not_93_out, not_94_out, not_95_out, not_96_out, not_97_out,
       not_98_out, not_99_out, not_100_out, not_101_out, not_102_out, not_103_out, not_104_out, not_105_out,
       not_106_out, not_107_out, not_108_out;

  not not_1 (not_1_out, op5);
  not not_2 (not_2_out, op4);
  not not_3 (not_3_out, op3);
  not not_4 (not_4_out, op2);
  not not_5 (not_5_out, op1);
  not not_6 (not_6_out, op0);
  not not_7 (not_7_out, func4);
  not not_8 (not_8_out, func3);
  not not_9 (not_9_out, func2);
  not not_10 (not_10_out, func1);
  not not_11 (not_11_out, func0);
  not not_12 (not_12_out, op5);
  not not_13 (not_13_out, op4);
  not not_14 (not_14_out, op3);
  not not_15 (not_15_out, op2);
  not not_16 (not_16_out, op1);
  not not_17 (not_17_out, op0);
  not not_18 (not_18_out, func4);
  not not_19 (not_19_out, func3);
  not not_20 (not_20_out, func2);
  not not_21 (not_21_out, func1);
  not not_22 (not_22_out, op5);
  not not_23 (not_23_out, op4);
  not not_24 (not_24_out, op3);
  not not_25 (not_25_out, op2);
  not not_26 (not_26_out, op1);
  not not_27 (not_27_out, op0);
  not not_28 (not_28_out, func4);
  not not_29 (not_29_out, func3);
  not not_30 (not_30_out, func1);
  not not_31 (not_31_out, func0);
  not not_32 (not_32_out, op5);
  not not_33 (not_33_out, op4);
  not not_34 (not_34_out, op3);
  not not_35 (not_35_out, op2);
  not not_36 (not_36_out, op1);
  not not_37 (not_37_out, op0);
  not not_38 (not_38_out, func5);
  not not_39 (not_39_out, func4);
  not not_40 (not_40_out, func3);
  not not_41 (not_41_out, func2);
  not not_42 (not_42_out, func1);
  not not_43 (not_43_out, func0);
  not not_44 (not_44_out, op5);
  not not_45 (not_45_out, op4);
  not not_46 (not_46_out, op3);
  not not_47 (not_47_out, op2);
  not not_48 (not_48_out, op1);
  not not_49 (not_49_out, op0);
  not not_50 (not_50_out, func5);
  not not_51 (not_51_out, func4);
  not not_52 (not_52_out, func3);
  not not_53 (not_53_out, func2);
  not not_54 (not_54_out, op5);
  not not_55 (not_55_out, op4);
  not not_56 (not_56_out, op3);
  not not_57 (not_57_out, op2);
  not not_58 (not_58_out, op1);
  not not_59 (not_59_out, op0);
  not not_60 (not_60_out, func4);
  not not_61 (not_61_out, func3);
  not not_62 (not_62_out, func2);
  not not_63 (not_63_out, func0);
  not not_64 (not_64_out, op5);
  not not_65 (not_65_out, op4);
  not not_66 (not_66_out, op3);
  not not_67 (not_67_out, op2);
  not not_68 (not_68_out, op1);
  not not_69 (not_69_out, op0);
  not not_70 (not_70_out, func4);
  not not_71 (not_71_out, func3);
  not not_72 (not_72_out, func1);
  not not_73 (not_73_out, op5);
  not not_74 (not_74_out, op4);
  not not_75 (not_75_out, op3);
  not not_76 (not_76_out, op2);
  not not_77 (not_77_out, op1);
  not not_78 (not_78_out, op0);
  not not_79 (not_79_out, func4);
  not not_80 (not_80_out, func3);
  not not_81 (not_81_out, op5);
  not not_82 (not_82_out, op4);
  not not_83 (not_83_out, op3);
  not not_84 (not_84_out, op2);
  not not_85 (not_85_out, op1);
  not not_86 (not_86_out, op0);
  not not_87 (not_87_out, func4);
  not not_88 (not_88_out, func2);
  not not_89 (not_89_out, func0);
  not not_90 (not_90_out, op5);
  not not_91 (not_91_out, op4);
  not not_92 (not_92_out, op3);
  not not_93 (not_93_out, op2);
  not not_94 (not_94_out, op1);
  not not_95 (not_95_out, op0);
  not not_96 (not_96_out, func4);
  not not_97 (not_97_out, func2);
  not not_98 (not_98_out, op5);
  not not_99 (not_99_out, op4);
  not not_100 (not_100_out, op3);
  not not_101 (not_101_out, op2);
  not not_102 (not_102_out, op1);
  not not_103 (not_103_out, op0);
  not not_104 (not_104_out, func5);
  not not_105 (not_105_out, func4);
  not not_106 (not_106_out, func2);
  not not_107 (not_107_out, func1);
  not not_108 (not_108_out, func0);
  and and_1 (add, not_1_out, not_2_out, not_3_out, not_4_out, not_5_out, not_6_out, func5, not_7_out, not_8_out, not_9_out, not_10_out, not_11_out);
  and and_2 (addu, not_12_out, not_13_out, not_14_out, not_15_out, not_16_out, not_17_out, func5, not_18_out, not_19_out, not_20_out, not_21_out, func0);
  and and_3 (\and , not_22_out, not_23_out, not_24_out, not_25_out, not_26_out, not_27_out, func5, not_28_out, not_29_out, func2, not_30_out, not_31_out);
  and and_4 (sll, not_32_out, not_33_out, not_34_out, not_35_out, not_36_out, not_37_out, not_38_out, not_39_out, not_40_out, not_41_out, not_42_out, not_43_out);
  and and_5 (sra, not_44_out, not_45_out, not_46_out, not_47_out, not_48_out, not_49_out, not_50_out, not_51_out, not_52_out, not_53_out, func1, func0);
  and and_6 (sub, not_54_out, not_55_out, not_56_out, not_57_out, not_58_out, not_59_out, func5, not_60_out, not_61_out, not_62_out, func1, not_63_out);
  and and_7 (\or , not_64_out, not_65_out, not_66_out, not_67_out, not_68_out, not_69_out, func5, not_70_out, not_71_out, func2, not_72_out, func0);
  and and_8 (\nor , not_73_out, not_74_out, not_75_out, not_76_out, not_77_out, not_78_out, func5, not_79_out, not_80_out, func2, func1, func0);
  and and_9 (slt, not_81_out, not_82_out, not_83_out, not_84_out, not_85_out, not_86_out, func5, not_87_out, func3, not_88_out, func1, not_89_out);
  and and_10 (sltu, not_90_out, not_91_out, not_92_out, not_93_out, not_94_out, not_95_out, func5, not_96_out, func3, not_97_out, func1, func0);
  and and_11 (jr, not_98_out, not_99_out, not_100_out, not_101_out, not_102_out, not_103_out, not_104_out, not_105_out, func3, not_106_out, not_107_out, not_108_out);
endmodule

module ctrl_2 (
  input  op5,
  input  op4,
  input  op3,
  input  op2,
  input  op1,
  input  op0,
  input  func5,
  input  func4,
  input  func3,
  input  func2,
  input  func1,
  input  func0,
  output srl,
  output addi,
  output addiu,
  output andi,
  output ori,
  output lw,
  output sw,
  output beq,
  output bne,
  output slti
);

  wire not_1_out, not_2_out, not_3_out, not_4_out, not_5_out, not_6_out, not_7_out, not_8_out, not_9_out,
       not_10_out, not_11_out, not_12_out, not_13_out, not_14_out, not_15_out, not_16_out, not_17_out,
       not_18_out, not_19_out, not_20_out, not_21_out, not_22_out, not_23_out, not_24_out, not_25_out,
       not_26_out, not_27_out, not_28_out, not_29_out, not_30_out, not_31_out, not_32_out, not_33_out,
       not_34_out, not_35_out, not_36_out, not_37_out, not_38_out, not_39_out, not_40_out, not_41_out,
       not_42_out, not_43_out, not_44_out, not_45_out;

  not not_1 (not_1_out, op5);
  not not_2 (not_2_out, op4);
  not not_3 (not_3_out, op3);
  not not_4 (not_4_out, op2);
  not not_5 (not_5_out, op1);
  not not_6 (not_6_out, op0);
  not not_7 (not_7_out, func5);
  not not_8 (not_8_out, func4);
  not not_9 (not_9_out, func3);
  not not_10 (not_10_out, func2);
  not not_11 (not_11_out, func0);
  not not_12 (not_12_out, op5);
  not not_13 (not_13_out, op4);
  not not_14 (not_14_out, op2);
  not not_15 (not_15_out, op1);
  not not_16 (not_16_out, op0);
  not not_17 (not_17_out, op5);
  not not_18 (not_18_out, op4);
  not not_19 (not_19_out, op2);
  not not_20 (not_20_out, op1);
  not not_21 (not_21_out, op5);
  not not_22 (not_22_out, op4);
  not not_23 (not_23_out, op1);
  not not_24 (not_24_out, op0);
  not not_25 (not_25_out, op5);
  not not_26 (not_26_out, op4);
  not not_27 (not_27_out, op1);
  not not_28 (not_28_out, op4);
  not not_29 (not_29_out, op3);
  not not_30 (not_30_out, op2);
  not not_31 (not_31_out, op4);
  not not_32 (not_32_out, op2);
  not not_33 (not_33_out, op5);
  not not_34 (not_34_out, op4);
  not not_35 (not_35_out, op3);
  not not_36 (not_36_out, op1);
  not not_37 (not_37_out, op0);
  not not_38 (not_38_out, op5);
  not not_39 (not_39_out, op4);
  not not_40 (not_40_out, op3);
  not not_41 (not_41_out, op1);
  not not_42 (not_42_out, op5);
  not not_43 (not_43_out, op4);
  not not_44 (not_44_out, op2);
  not not_45 (not_45_out, op0);
  and and_1 (srl, not_1_out, not_2_out, not_3_out, not_4_out, not_5_out, not_6_out, not_7_out, not_8_out, not_9_out, not_10_out, func1, not_11_out);
  and and_2 (addi, not_12_out, not_13_out, op3, not_14_out, not_15_out, not_16_out);
  and and_3 (addiu, not_17_out, not_18_out, op3, not_19_out, not_20_out, op0);
  and and_4 (andi, not_21_out, not_22_out, op3, op2, not_23_out, not_24_out);
  and and_5 (ori, not_25_out, not_26_out, op3, op2, not_27_out, op0);
  and and_6 (lw, op5, not_28_out, not_29_out, not_30_out, op1, op0);
  and and_7 (sw, op5, not_31_out, op3, not_32_out, op1, op0);
  and and_8 (beq, not_33_out, not_34_out, not_35_out, op2, not_36_out, not_37_out);
  and and_9 (bne, not_38_out, not_39_out, not_40_out, op2, not_41_out, op0);
  and and_10 (slti, not_42_out, not_43_out, op3, not_44_out, op1, not_45_out);
endmodule

module ctrl_3 (
  input  op5,
  input  op4,
  input  op3,
  input  op2,
  input  op1,
  input  op0,
  input  func5,
  input  func4,
  input  func3,
  input  func2,
  input  func1,
  input  func0,
  output j,
  output jal,
  output syscall,
  output \xor ,
  output xori,
  output lbu,
  output bgtz
);

  wire not_1_out, not_2_out, not_3_out, not_4_out, not_5_out, not_6_out, not_7_out, not_8_out, not_9_out,
       not_10_out, not_11_out, not_12_out, not_13_out, not_14_out, not_15_out, not_16_out, not_17_out,
       not_18_out, not_19_out, not_20_out, not_21_out, not_22_out, not_23_out, not_24_out, not_25_out,
       not_26_out, not_27_out, not_28_out, not_29_out, not_30_out, not_31_out, not_32_out, not_33_out,
       not_34_out, not_35_out, not_36_out, not_37_out, not_38_out;

  not not_1 (not_1_out, op5);
  not not_2 (not_2_out, op4);
  not not_3 (not_3_out, op3);
  not not_4 (not_4_out, op2);
  not not_5 (not_5_out, op0);
  not not_6 (not_6_out, op5);
  not not_7 (not_7_out, op4);
  not not_8 (not_8_out, op3);
  not not_9 (not_9_out, op2);
  not not_10 (not_10_out, op5);
  not not_11 (not_11_out, op4);
  not not_12 (not_12_out, op3);
  not not_13 (not_13_out, op2);
  not not_14 (not_14_out, op1);
  not not_15 (not_15_out, op0);
  not not_16 (not_16_out, func5);
  not not_17 (not_17_out, func4);
  not not_18 (not_18_out, func1);
  not not_19 (not_19_out, func0);
  not not_20 (not_20_out, op5);
  not not_21 (not_21_out, op4);
  not not_22 (not_22_out, op3);
  not not_23 (not_23_out, op2);
  not not_24 (not_24_out, op1);
  not not_25 (not_25_out, op0);
  not not_26 (not_26_out, func4);
  not not_27 (not_27_out, func3);
  not not_28 (not_28_out, func0);
  not not_29 (not_29_out, op5);
  not not_30 (not_30_out, op4);
  not not_31 (not_31_out, op0);
  not not_32 (not_32_out, op4);
  not not_33 (not_33_out, op3);
  not not_34 (not_34_out, op1);
  not not_35 (not_35_out, op0);
  not not_36 (not_36_out, op5);
  not not_37 (not_37_out, op4);
  not not_38 (not_38_out, op3);
  and and_1 (j, not_1_out, not_2_out, not_3_out, not_4_out, op1, not_5_out);
  and and_2 (jal, not_6_out, not_7_out, not_8_out, not_9_out, op1, op0);
  and and_3 (syscall, not_10_out, not_11_out, not_12_out, not_13_out, not_14_out, not_15_out, not_16_out, not_17_out, func3, func2, not_18_out, not_19_out);
  and and_4 (\xor , not_20_out, not_21_out, not_22_out, not_23_out, not_24_out, not_25_out, func5, not_26_out, not_27_out, func2, func1, not_28_out);
  and and_5 (xori, not_29_out, not_30_out, op3, op2, op1, not_31_out);
  and and_6 (lbu, op5, not_32_out, not_33_out, op2, not_34_out, not_35_out);
  and and_7 (bgtz, not_36_out, not_37_out, not_38_out, op2, op1, op0);
endmodule

module selector (
  input  [3:0] RF_R1,
  input  [2:0] RF_R2,
  input  [2:0] S_EXT,
  input  [25:0] _26bitInput,
  output [4:0] RF_R1_OUT,
  output [31:0] S_EXT_OUTPUT,
  output [4:0] RF_R2_OUT
);

  wire [1:0] priority_encoder_1_out, priority_encoder_2_out, priority_encoder_3_out;
  wire [31:0] _26to32extend, bit_extender_1_out, bit_extender_2_out;

  Priority_Encoder #(.select(2)) priority_encoder_1 (
    .in0(1'b1), .in1(RF_R2[2]), .in2(RF_R2[1]), .in3(RF_R2[0]), .out(priority_encoder_1_out));  // open: gs, en_out, en_in
  Priority_Encoder #(.select(2), .disabled(0)) priority_encoder_2 (
    .in0(RF_R1[3]), .in1(RF_R1[0]), .in2(RF_R1[1]), .in3(RF_R1[2]), .out(priority_encoder_2_out));  // open: gs, en_out, en_in
  Multiplexer #(.select(2), .width(5), .disabled(0), .enable("false")) multiplexer_1 (
    .in0({5{1'b0}}), .in1(_26bitInput[20:16]), .in2(5'b00010), .in3(_26bitInput[25:21]), .out(RF_R1_OUT),
    .sel(priority_encoder_2_out));
  Multiplexer #(.select(2), .width(5), .enable("false")) multiplexer_2 (
    .in0({5{1'b0}}), .in1(_26bitInput[20:16]), .in2(5'b00100), .in3(_26bitInput[25:21]), .out(RF_R2_OUT),
    .sel(priority_encoder_1_out));
  Pull_Resistor pull_resistor_1 (.node(priority_encoder_2_out));
  assign bit_extender_1_out = {{27{1'b0}}, _26bitInput[10:6]};  // Bit_Extender bit_extender_1
  assign bit_extender_2_out = {{16{_26bitInput[15]}}, _26bitInput[15:0]};  // Bit_Extender bit_extender_2
  Priority_Encoder #(.select(2), .disabled(0)) priority_encoder_3 (
    .in0(1'b1), .in1(S_EXT[0]), .in2(S_EXT[1]), .in3(S_EXT[2]), .out(priority_encoder_3_out));  // open: gs, en_out, en_in
  Multiplexer #(.select(2), .width(32), .disabled(0), .enable("false")) multiplexer_3 (
    .in0({32{1'b0}}), .in1(bit_extender_1_out), .in2(bit_extender_2_out), .in3(_26to32extend),
    .out(S_EXT_OUTPUT), .sel(priority_encoder_3_out));
  assign _26to32extend = {{4{_26bitInput[25]}}, {_26bitInput, 2'b00}};  // Bit_Extender bit_extender_3

  // Other names for the same wires on the sheet: _16Immediate[15:0] = _26bitInput[15:0];
  //   _26Immediate[25:0] = _26bitInput; _28Immediate[27:2] = _26bitInput; func[5:0] = _26bitInput[5:0];
  //   instructionInput[25:0] = _26bitInput; shmat[4:0] = _26bitInput[10:6]; RD[4:0] = _26bitInput[15:11];
  //   RT[4:0] = _26bitInput[20:16]; RS[4:0] = _26bitInput[25:21]; R1_rt = RF_R1[0]; R1_2 = RF_R1[1]; R1_rs = RF_R1[2];
  //   R1_0 = RF_R1[3]; R2_rs = RF_R2[0]; R2_4 = RF_R2[1]; R2_rt = RF_R2[2]; S_EXT_shmat = S_EXT[0];
  //   S_EXT_IMM15 = S_EXT[1]; S_EXT_IMM25 = S_EXT[2]
endmodule

module \if  (
  input  rst,
  input  clk,
  input  en,
  input  [31:0] in,
  input  [31:0] PC_in,
  input  clear,
  input  [31:0] PCp4_in,
  output [31:0] PC_out,
  output [31:0] out,
  output [31:0] PCp4_out
);

  wire clear_t;
  wire [31:0] multiplexer_1_out, multiplexer_2_out, multiplexer_3_out;

  Multiplexer #(.width(32), .enable("false")) multiplexer_1 (
    .in0({32{1'b0}}), .in1(PCp4_in), .out(multiplexer_1_out), .sel(clear_t));
  not not_1 (clear_t, clear);
  Multiplexer #(.width(32), .enable("false")) multiplexer_2 (
    .in0({32{1'b0}}), .in1(in), .out(multiplexer_2_out), .sel(clear_t));
  Pull_Resistor #(.pull(1)) pull_resistor_1 (.node(en));
  Pull_Resistor #(.pull(1)) pull_resistor_2 (.node(en));
  Register #(.width(32)) register_1 (.D(multiplexer_2_out), .en(en), .Q(out), .clk(clk), .clr(rst));
  Multiplexer #(.width(32), .enable("false")) multiplexer_3 (
    .in0({32{1'b0}}), .in1(PC_in), .out(multiplexer_3_out), .sel(clear_t));
  Register #(.width(32)) register_2 (.D(multiplexer_1_out), .en(en), .Q(PCp4_out), .clk(clk), .clr(rst));
  Register #(.width(32)) register_3 (.D(multiplexer_3_out), .en(en), .Q(PC_out), .clk(clk), .clr(rst));

  // Notes on the sheet:
  //   输入
  //   输出
endmodule

module id (
  input  [3:0] OP,
  input  [2:0] R2,
  input  en,
  input  rst,
  input  clk,
  input  [1:0] dm,
  input  [1:0] ALUB,
  input  [31:0] A_in,
  input  [31:0] ext,
  input  [31:0] B_in,
  input  clear,
  input  [4:0] RA,
  input  [4:0] RB,
  input  [1:0] srcOP,
  input  [2:0] rf_in,
  input  [31:0] PC_in,
  input  lbu_in,
  input  [25:0] instr26_in,
  input  [2:0] rfw_in,
  input  [1:0] PCctrl_in,
  input  [1:0] temp_in,
  input  [31:0] PCp4_in,
  input  [3:0] branch,
  input  loadUse_in,
  output [1:0] dm_out,
  output [1:0] ALUB_out,
  output [31:0] A_out,
  output [31:0] ext_2,
  output [31:0] B_in_2,
  output [3:0] OP_2,
  output [2:0] R2_2,
  output [4:0] RA_out,
  output [4:0] RB_out,
  output [1:0] srcOP_out,
  output [2:0] rfdin_out,
  output [31:0] PC_out,
  output lbu_out,
  output [25:0] instr26_out,
  output [2:0] rfw_out,
  output [1:0] PCctrl_out,
  output [1:0] temp_out,
  output [31:0] PCp4_out,
  output [3:0] branch_out,
  output loadUser_out
);

  wire clear_t, multiplexer_13_out, multiplexer_20_out;
  wire [1:0] multiplexer_1_out, multiplexer_2_out, multiplexer_10_out, multiplexer_16_out, multiplexer_17_out;
  wire [2:0] multiplexer_7_out, multiplexer_12_out, multiplexer_15_out;
  wire [3:0] multiplexer_6_out, multiplexer_19_out;
  wire [4:0] multiplexer_8_out, multiplexer_9_out;
  wire [25:0] multiplexer_14_out;
  wire [31:0] multiplexer_3_out, multiplexer_4_out, multiplexer_5_out, multiplexer_11_out, multiplexer_18_out;

  Multiplexer #(.width(2), .enable("false")) multiplexer_1 (
    .in0(2'b00), .in1(dm), .out(multiplexer_1_out), .sel(clear_t));
  Multiplexer #(.width(2), .enable("false")) multiplexer_2 (
    .in0(2'b00), .in1(ALUB), .out(multiplexer_2_out), .sel(clear_t));
  Multiplexer #(.width(32), .enable("false")) multiplexer_3 (
    .in0({32{1'b0}}), .in1(A_in), .out(multiplexer_3_out), .sel(clear_t));
  Multiplexer #(.width(32), .enable("false")) multiplexer_4 (
    .in0({32{1'b0}}), .in1(ext), .out(multiplexer_4_out), .sel(clear_t));
  Multiplexer #(.width(32), .enable("false")) multiplexer_5 (
    .in0({32{1'b0}}), .in1(B_in), .out(multiplexer_5_out), .sel(clear_t));
  Multiplexer #(.width(4), .enable("false")) multiplexer_6 (
    .in0(4'b0000), .in1(OP), .out(multiplexer_6_out), .sel(clear_t));
  Multiplexer #(.width(3), .enable("false")) multiplexer_7 (
    .in0(3'b000), .in1(R2), .out(multiplexer_7_out), .sel(clear_t));
  Multiplexer #(.width(5), .enable("false")) multiplexer_8 (
    .in0({5{1'b0}}), .in1(RA), .out(multiplexer_8_out), .sel(clear_t));
  Multiplexer #(.width(5), .enable("false")) multiplexer_9 (
    .in0({5{1'b0}}), .in1(RB), .out(multiplexer_9_out), .sel(clear_t));
  Multiplexer #(.width(2), .enable("false")) multiplexer_10 (
    .in0(2'b00), .in1(srcOP), .out(multiplexer_10_out), .sel(clear_t));
  not not_1 (clear_t, clear);
  Pull_Resistor #(.pull(1)) pull_resistor_1 (.node(en));
  Multiplexer #(.width(32), .enable("false")) multiplexer_11 (
    .in0({32{1'b0}}), .in1(PC_in), .out(multiplexer_11_out), .sel(clear_t));
  Multiplexer #(.width(3), .enable("false")) multiplexer_12 (
    .in0(3'b000), .in1(rf_in), .out(multiplexer_12_out), .sel(clear_t));
  Multiplexer #(.enable("false")) multiplexer_13 (.in0(1'b0), .in1(lbu_in), .out(multiplexer_13_out), .sel(clear_t));
  Multiplexer #(.width(26), .enable("false")) multiplexer_14 (
    .in0({26{1'b0}}), .in1(instr26_in), .out(multiplexer_14_out), .sel(clear_t));
  Multiplexer #(.width(3), .enable("false")) multiplexer_15 (
    .in0(3'b000), .in1(rfw_in), .out(multiplexer_15_out), .sel(clear_t));
  Multiplexer #(.width(2), .enable("false")) multiplexer_16 (
    .in0(2'b00), .in1(PCctrl_in), .out(multiplexer_16_out), .sel(clear_t));
  Multiplexer #(.width(2), .enable("false")) multiplexer_17 (
    .in0(2'b00), .in1(temp_in), .out(multiplexer_17_out), .sel(clear_t));
  Multiplexer #(.width(32), .enable("false")) multiplexer_18 (
    .in0({32{1'b0}}), .in1(PCp4_in), .out(multiplexer_18_out), .sel(clear_t));
  Multiplexer #(.width(4), .enable("false")) multiplexer_19 (
    .in0(4'b0000), .in1(branch), .out(multiplexer_19_out), .sel(clear_t));
  Multiplexer #(.enable("false")) multiplexer_20 (
    .in0(1'b0), .in1(loadUse_in), .out(multiplexer_20_out), .sel(clear_t));
  Register #(.width(2)) register_1 (.D(multiplexer_1_out), .en(en), .Q(dm_out), .clk(clk), .clr(rst));
  Register #(.width(2)) register_2 (.D(multiplexer_2_out), .en(en), .Q(ALUB_out), .clk(clk), .clr(rst));
  Register #(.width(32)) register_3 (.D(multiplexer_3_out), .en(en), .Q(A_out), .clk(clk), .clr(rst));
  Register #(.width(32)) register_4 (.D(multiplexer_4_out), .en(en), .Q(ext_2), .clk(clk), .clr(rst));
  Register #(.width(32)) register_5 (.D(multiplexer_5_out), .en(en), .Q(B_in_2), .clk(clk), .clr(rst));
  Register #(.width(4)) register_6 (.D(multiplexer_6_out), .en(en), .Q(OP_2), .clk(clk), .clr(rst));
  Register #(.width(3)) register_7 (.D(multiplexer_7_out), .en(en), .Q(R2_2), .clk(clk), .clr(rst));
  Register #(.width(5)) register_8 (.D(multiplexer_8_out), .en(en), .Q(RA_out), .clk(clk), .clr(rst));
  Register #(.width(5)) register_9 (.D(multiplexer_9_out), .en(en), .Q(RB_out), .clk(clk), .clr(rst));
  Register #(.width(2)) register_10 (.D(multiplexer_10_out), .en(en), .Q(srcOP_out), .clk(clk), .clr(rst));
  Register #(.width(32)) register_11 (.D(multiplexer_11_out), .en(en), .Q(PC_out), .clk(clk), .clr(rst));
  Register #(.width(3)) register_12 (.D(multiplexer_12_out), .en(en), .Q(rfdin_out), .clk(clk), .clr(rst));
  Register #(.width(1)) register_13 (.D(multiplexer_13_out), .en(en), .Q(lbu_out), .clk(clk), .clr(rst));
  Register #(.width(26)) register_14 (.D(multiplexer_14_out), .en(en), .Q(instr26_out), .clk(clk), .clr(rst));
  Register #(.width(3)) register_15 (.D(multiplexer_15_out), .en(en), .Q(rfw_out), .clk(clk), .clr(rst));
  Register #(.width(2)) register_16 (.D(multiplexer_16_out), .en(en), .Q(PCctrl_out), .clk(clk), .clr(rst));
  Register #(.width(2)) register_17 (.D(multiplexer_17_out), .en(en), .Q(temp_out), .clk(clk), .clr(rst));
  Register #(.width(32)) register_18 (.D(multiplexer_18_out), .en(en), .Q(PCp4_out), .clk(clk), .clr(rst));
  Register #(.width(4)) register_19 (.D(multiplexer_19_out), .en(en), .Q(branch_out), .clk(clk), .clr(rst));
  Register #(.width(1)) register_20 (.D(multiplexer_20_out), .en(en), .Q(loadUser_out), .clk(clk), .clr(rst));

  // Other names for the same wires on the sheet: Ain[31:0] = A_in; ALU_B[1:0] = ALUB; B[31:0] = B_in;
  //   B_out[31:0] = B_in_2; ext_out[31:0] = ext_2; OP_out[3:0] = OP_2; PC_ctrl_in[1:0] = PCctrl_in;
  //   R2_out[2:0] = R2_2

  // Notes on the sheet:
  //   输入
  //   输出
endmodule

module ex (
  input  [1:0] dm,
  input  [31:0] result,
  input  rst,
  input  clk,
  input  \end ,
  input  en,
  input  [31:0] Bin,
  input  [2:0] rf_in,
  input  [31:0] PC_in,
  input  lbu_in,
  input  [2:0] rfw_in,
  input  [25:0] instr26_in,
  input  [4:0] RA,
  input  [4:0] RB,
  input  [1:0] srcOP,
  input  loadUse_in,
  output [1:0] dm_out,
  output [31:0] result_out,
  output end_out,
  output [31:0] Bin_out,
  output [2:0] rfdin_out,
  output [31:0] PC_out,
  output lbu_out,
  output [2:0] rfw_out,
  output [25:0] instr26_out,
  output [4:0] RA_out,
  output [4:0] RB_out,
  output [1:0] srcOP_out,
  output loadUser_out
);

  wire clear, multiplexer_1_out;

  Pull_Resistor #(.pull(1)) pull_resistor_1 (.node(en));
  Multiplexer #(.enable("false")) multiplexer_1 (.in0(1'b0), .in1(loadUse_in), .out(multiplexer_1_out), .sel(clear));
  Register #(.width(2)) register_1 (.D(dm), .en(en), .Q(dm_out), .clk(clk), .clr(rst));
  Register #(.width(32)) register_2 (.D(result), .en(en), .Q(result_out), .clk(clk), .clr(rst));
  Register #(.width(1)) register_3 (.D(\end ), .en(en), .Q(end_out), .clk(clk), .clr(rst));
  Register #(.width(32)) register_4 (.D(Bin), .en(en), .Q(Bin_out), .clk(clk), .clr(rst));
  Register #(.width(5)) register_5 (.D(RA), .en(en), .Q(RA_out), .clk(clk), .clr(rst));
  Register #(.width(5)) register_6 (.D(RB), .en(en), .Q(RB_out), .clk(clk), .clr(rst));
  Register #(.width(2)) register_7 (.D(srcOP), .en(en), .Q(srcOP_out), .clk(clk), .clr(rst));
  Register #(.width(1)) register_8 (.D(multiplexer_1_out), .en(en), .Q(loadUser_out), .clk(clk), .clr(rst));
  Register #(.width(32)) register_9 (.D(PC_in), .en(en), .Q(PC_out), .clk(clk), .clr(rst));
  Register #(.width(26)) register_10 (.D(instr26_in), .en(en), .Q(instr26_out), .clk(clk), .clr(rst));
  Register #(.width(3)) register_11 (.D(rf_in), .en(en), .Q(rfdin_out), .clk(clk), .clr(rst));
  Register #(.width(1)) register_12 (.D(lbu_in), .en(en), .Q(lbu_out), .clk(clk), .clr(rst));
  Register #(.width(3)) register_13 (.D(rfw_in), .en(en), .Q(rfw_out), .clk(clk), .clr(rst));

  // Other names for the same wires on the sheet: equal = \end 

  // Notes on the sheet:
  //   输入
  //   输出
endmodule

module mem (
  input  en,
  input  rst,
  input  clk,
  input  syscall,
  input  WE,
  input  [31:0] writeBack_out,
  input  [4:0] rw,
  output syscall_out,
  output WE_out,
  output [31:0] writeBack_out_2,
  output [4:0] rw_out
);

  Pull_Resistor #(.pull(1)) pull_resistor_1 (.node(en));
  Register #(.width(1)) register_1 (.D(syscall), .en(en), .Q(syscall_out), .clk(clk), .clr(rst));
  Register #(.width(1)) register_2 (.D(WE), .en(en), .Q(WE_out), .clk(clk), .clr(rst));
  Register #(.width(32)) register_3 (.D(writeBack_out), .en(en), .Q(writeBack_out_2), .clk(clk), .clr(rst));
  Register #(.width(5)) register_4 (.D(rw), .en(en), .Q(rw_out), .clk(clk), .clr(rst));

  // Other names for the same wires on the sheet: writeBack[31:0] = writeBack_out;
  //   writeBack_out_t[31:0] = writeBack_out_2

  // Notes on the sheet:
  //   输入
  //   输出
endmodule

module npc (
  input  [3:0] PC_ctrl,
  input  [31:0] PC_in,
  input  [31:0] oldPC_4,
  input  [25:0] _26bitInput,
  input  [31:0] RF_D1,
  output [31:0] PC_out,
  output [31:0] PC_4,
  output JMP
);

  wire adder_1_cout, adder_2_cout;
  wire [1:0] priority_encoder_1_out;
  wire [31:0] adder_2_out, bit_extender_1_out;

  assign bit_extender_1_out = {{14{_26bitInput[15]}}, {_26bitInput[15:0], 2'b00}};  // Bit_Extender bit_extender_1
  Adder #(.width(32)) adder_1 (.a(PC_in), .b(32'h4), .out(PC_4), .cout(adder_1_cout));  // open: cin
  Priority_Encoder #(.select(2)) priority_encoder_1 (
    .in0(PC_ctrl[3]), .in1(PC_ctrl[2]), .in2(PC_ctrl[1]), .in3(PC_ctrl[0]), .out(priority_encoder_1_out));  // open: gs, en_out, en_in
  Adder #(.width(32)) adder_2 (
    .a(oldPC_4), .b(bit_extender_1_out), .out(adder_2_out), .cout(adder_2_cout));  // open: cin
  Pull_Resistor pull_resistor_1 (.node(priority_encoder_1_out));
  Multiplexer #(.select(2), .width(32), .disabled(0), .enable("false")) multiplexer_1 (
    .in0(PC_4), .in1(adder_2_out), .in2({PC_in[31:28], _26bitInput, 2'b00}), .in3(RF_D1), .out(PC_out),
    .sel(priority_encoder_1_out));
  or or_1 (JMP, PC_ctrl[2], PC_ctrl[1], PC_ctrl[0]);
  // also tied to GND on the sheet: {adder_1_cout, adder_2_cout}

  // Other names for the same wires on the sheet: _16Immediate[15:0] = _26bitInput[15:0];
  //   _26Immediate[25:0] = _26bitInput; _28Immediate[27:2] = _26bitInput; instructionInput[25:0] = _26bitInput;
  //   PC[31:0] = PC_in; PC_RF_D1 = PC_ctrl[0]; PC_0XF0000000__addr = PC_ctrl[1]; PC_offset = PC_ctrl[2];
  //   pc_PC_4 = PC_ctrl[3]
endmodule

module wb (
  input  [2:0] RF_Din,
  input  LBU,
  input  [31:0] DM_OUT,
  input  [31:0] ALU,
  input  [2:0] RF_W,
  input  [31:0] PC_in,
  input  [25:0] _26bitInput,
  output [4:0] RF_W_OUT,
  output WE,
  output [31:0] RF_Din_OUTPUT
);

  wire [1:0] priority_encoder_1_out, priority_encoder_2_out;
  wire [31:0] adder_1_out;

  Adder #(.width(32)) adder_1 (.a(32'h4), .b(PC_in), .out(adder_1_out));  // open: cin, cout
  Priority_Encoder #(.select(2)) priority_encoder_1 (
    .in0(RF_Din[2]), .in1(RF_Din[1]), .in2(RF_Din[0]), .in3(LBU), .out(priority_encoder_1_out));  // open: gs, en_out, en_in
  Multiplexer #(.select(2), .width(32), .disabled(0), .enable("false")) multiplexer_1 (
    .in0(ALU), .in1(DM_OUT), .in2(adder_1_out), .in3({{24{1'b0}}, DM_OUT[7:0]}), .out(RF_Din_OUTPUT),
    .sel(priority_encoder_1_out));
  or or_1 (WE, RF_W[2], RF_W[1], RF_W[0]);
  Priority_Encoder #(.select(2), .disabled(0)) priority_encoder_2 (
    .in0(1'b1), .in1(RF_W[0]), .in2(RF_W[1]), .in3(RF_W[2]), .out(priority_encoder_2_out));  // open: gs, en_out, en_in
  Multiplexer #(.select(2), .width(5), .disabled(0), .enable("false")) multiplexer_2 (
    .in0({5{1'b0}}), .in1({5{1'b1}}), .in2(_26bitInput[15:11]), .in3(_26bitInput[20:16]), .out(RF_W_OUT),
    .sel(priority_encoder_2_out));

  // Other names for the same wires on the sheet: _16Immediate[15:0] = _26bitInput[15:0];
  //   _26Immediate[25:0] = _26bitInput; func[5:0] = _26bitInput[5:0]; instructionInput[25:0] = _26bitInput;
  //   shmat[4:0] = _26bitInput[10:6]; RD[4:0] = _26bitInput[15:11]; RT[4:0] = _26bitInput[20:16];
  //   RS[4:0] = _26bitInput[25:21]; PC[31:0] = PC_in; Din_PC_4 = RF_Din[0]; Din_DM_out = RF_Din[1];
  //   Din_ALU = RF_Din[2]; W_31 = RF_W[0]; W_rd = RF_W[1]; W_rt = RF_W[2]
endmodule

// conflict detect
module conflict_dectect (
  input  [4:0] RA,
  input  [4:0] RB,
  input  [1:0] srcOP,
  input  WE1,
  input  WE2,
  input  [4:0] rw1,
  input  [4:0] rw2,
  output B_W1,
  output B_W2,
  output conflict,
  output A_W1,
  output A_W2
);

  wire and_1_out, and_2_out, and_3_out, and_4_out, and_9_out, and_10_out, and_11_out, and_12_out, and_13_out,
       and_14_out, comparator_1_eq, comparator_2_eq, comparator_3_eq, comparator_4_eq, comparator_5_eq,
       comparator_6_eq, comparator_7_eq, comparator_8_eq, comparator_9_eq, comparator_10_eq,
       comparator_11_eq, comparator_12_eq, comparator_13_eq, comparator_14_eq, comparator_15_eq,
       comparator_16_eq, or_1_out, or_2_out;

  Comparator #(.width(5)) comparator_1 (.a({5{1'b0}}), .b(rw1), .eq(comparator_1_eq));  // open: gt, lt
  Comparator #(.width(5)) comparator_2 (.a({5{1'b0}}), .b(rw2), .eq(comparator_2_eq));  // open: gt, lt
  Comparator #(.width(5)) comparator_3 (.a({5{1'b0}}), .b(rw1), .eq(comparator_3_eq));  // open: gt, lt
  Comparator #(.width(5)) comparator_4 (.a({5{1'b0}}), .b(rw2), .eq(comparator_4_eq));  // open: gt, lt
  Comparator #(.width(5)) comparator_5 (.a(RB), .b(rw1), .eq(comparator_5_eq));  // open: gt, lt
  Comparator #(.width(5)) comparator_6 (.a(RB), .b(rw2), .eq(comparator_6_eq));  // open: gt, lt
  Comparator #(.width(5)) comparator_7 (.a(RA), .b(rw1), .eq(comparator_7_eq));  // open: gt, lt
  Comparator #(.width(5)) comparator_8 (.a(RA), .b(rw2), .eq(comparator_8_eq));  // open: gt, lt
  and and_1 (and_1_out, WE1, ~comparator_1_eq, comparator_5_eq);  // AND_Gate
  and and_2 (and_2_out, WE2, ~comparator_2_eq, comparator_6_eq);  // AND_Gate
  and and_3 (and_3_out, WE1, ~comparator_3_eq, comparator_7_eq);  // AND_Gate
  and and_4 (and_4_out, WE2, ~comparator_4_eq, comparator_8_eq);  // AND_Gate
  and and_5 (B_W1, and_1_out, srcOP[1]);
  and and_6 (B_W2, and_2_out, srcOP[1]);
  and and_7 (A_W1, and_3_out, srcOP[0]);
  and and_8 (A_W2, and_4_out, srcOP[0]);
  Comparator #(.width(5)) comparator_9 (.a({5{1'b0}}), .b(rw2), .eq(comparator_9_eq));  // open: gt, lt
  Comparator #(.width(5)) comparator_10 (.a({5{1'b0}}), .b(rw1), .eq(comparator_10_eq));  // open: gt, lt
  Comparator #(.width(5)) comparator_11 (.a({5{1'b0}}), .b(rw2), .eq(comparator_11_eq));  // open: gt, lt
  Comparator #(.width(5)) comparator_12 (.a({5{1'b0}}), .b(rw1), .eq(comparator_12_eq));  // open: gt, lt
  Comparator #(.width(5)) comparator_13 (.a(RB), .b(rw1), .eq(comparator_13_eq));  // open: gt, lt
  Comparator #(.width(5)) comparator_14 (.a(RB), .b(rw2), .eq(comparator_14_eq));  // open: gt, lt
  Comparator #(.width(5)) comparator_15 (.a(RA), .b(rw1), .eq(comparator_15_eq));  // open: gt, lt
  Comparator #(.width(5)) comparator_16 (.a(RA), .b(rw2), .eq(comparator_16_eq));  // open: gt, lt
  and and_9 (and_9_out, WE1, ~comparator_12_eq, comparator_13_eq);  // AND_Gate
  and and_10 (and_10_out, WE2, ~comparator_9_eq, comparator_14_eq);  // AND_Gate
  and and_11 (and_11_out, WE1, ~comparator_10_eq, comparator_15_eq);  // AND_Gate
  and and_12 (and_12_out, WE2, ~comparator_11_eq, comparator_16_eq);  // AND_Gate
  or or_1 (or_1_out, and_9_out, and_10_out);
  or or_2 (or_2_out, and_11_out, and_12_out);
  and and_13 (and_13_out, or_1_out, srcOP[1]);
  and and_14 (and_14_out, or_2_out, srcOP[0]);
  or or_3 (conflict, and_13_out, and_14_out);

  // Other names for the same wires on the sheet: srcA = srcOP[0]; srcB = srcOP[1]

  // Notes on the sheet:
  //   当前的源操作数是否与后两个的目的操作数相同
endmodule

module WE_RW (
  input  [2:0] RF_W,
  input  [25:0] _26bitInput,
  output [4:0] RF_W_OUT,
  output WE
);

  wire [1:0] priority_encoder_1_out;

  or or_1 (WE, RF_W[2], RF_W[1], RF_W[0]);
  Priority_Encoder #(.select(2), .disabled(0)) priority_encoder_1 (
    .in0(1'b1), .in1(RF_W[0]), .in2(RF_W[1]), .in3(RF_W[2]), .out(priority_encoder_1_out));  // open: gs, en_out, en_in
  Multiplexer #(.select(2), .width(5), .disabled(0), .enable("false")) multiplexer_1 (
    .in0({5{1'b0}}), .in1({5{1'b1}}), .in2(_26bitInput[15:11]), .in3(_26bitInput[20:16]), .out(RF_W_OUT),
    .sel(priority_encoder_1_out));

  // Other names for the same wires on the sheet: _16Immediate[15:0] = _26bitInput[15:0];
  //   _26Immediate[25:0] = _26bitInput; func[5:0] = _26bitInput[5:0]; instructionInput[25:0] = _26bitInput;
  //   shmat[4:0] = _26bitInput[10:6]; RD[4:0] = _26bitInput[15:11]; RT[4:0] = _26bitInput[20:16];
  //   RS[4:0] = _26bitInput[25:21]; W_31 = RF_W[0]; W_rd = RF_W[1]; W_rt = RF_W[2]
endmodule

module PCctrl (
  input  ALU_equal,
  input  BGTZ,
  input  [3:0] branch,
  output \条件分支 ,
  output [1:0] PC_23
);

  wire and_1_out, and_2_out, and_3_out, and_4_out, and_5_out, and_6_out, not_1_out, not_2_out, not_3_out;

  not not_1 (not_1_out, ALU_equal);
  not not_2 (not_2_out, BGTZ);
  not not_3 (not_3_out, ALU_equal);
  and and_1 (and_1_out, branch[0], not_1_out);
  and and_2 (and_2_out, branch[1], ALU_equal);
  and and_3 (and_3_out, branch[2], not_2_out);
  and and_4 (and_4_out, branch[0], ALU_equal);
  and and_5 (and_5_out, branch[1], not_3_out);
  and and_6 (and_6_out, branch[2], BGTZ);
  or or_1 (PC_23[1], and_1_out, and_2_out, and_3_out, branch[3]);
  or or_2 (PC_23[0], and_4_out, and_5_out, and_6_out);

  assign \条件分支  = PC_23[0];

  // Other names for the same wires on the sheet: biggerThan0 = BGTZ; beq = branch[0]; bne = branch[1];
  //   BGTZ_t = branch[2]; PC_4 = branch[3]; PC_offset = PC_23[0]; 有条件分支成功跳转 = PC_23[0]; pc_PC_4 = PC_23[1]
endmodule

module redirect (
  input  B_W1,
  input  B_W2,
  input  A_W1,
  input  A_W2,
  input  [31:0] A,
  input  [31:0] B,
  input  [31:0] wb2,
  input  [31:0] wb1,
  output [31:0] redir_Aout,
  output [31:0] redir_Bout
);

  wire [31:0] multiplexer_1_out, multiplexer_3_out;

  Multiplexer #(.width(32), .enable("false")) multiplexer_1 (.in0(A), .in1(wb2), .out(multiplexer_1_out), .sel(A_W2));
  Multiplexer #(.width(32), .enable("false")) multiplexer_2 (
    .in0(multiplexer_1_out), .in1(wb1), .out(redir_Aout), .sel(A_W1));
  Multiplexer #(.width(32), .enable("false")) multiplexer_3 (.in0(B), .in1(wb2), .out(multiplexer_3_out), .sel(B_W2));
  Multiplexer #(.width(32), .enable("false")) multiplexer_4 (
    .in0(multiplexer_3_out), .in1(wb1), .out(redir_Bout), .sel(B_W1));
endmodule
